// Digital circuit VGA.dig as structural Verilog
module VGA (
  input  Clock_global,
  output hsync,
  output vsync,
  output video_on,
  output [9:0] hcount,
  output [9:0] vcount
);

  vga_sync #(.applicationType("IVERILOG")) u_vga_sync (
    .clk(Clock_global), .hsync(hsync), .vsync(vsync), .video_on(video_on), .hcount(hcount), .vcount(vcount));

  // Other names for the same wires on the sheet: clk = Clock_global

  // Notes on the sheet:
  //   Clock_global: Hz: 2147483647
endmodule

/* Code of vga_sync:
module vga_sync(
    input clk,
    output hsync,
    output vsync,
    output video_on,
    output [9:0] hcount,
    output [9:0] vcount
);

    parameter H_DISPLAY = 640;
    parameter H_FRONT   = 16;
    parameter H_SYNC    = 96;
    parameter H_BACK    = 48;
    parameter H_TOTAL   = 800;

    parameter V_DISPLAY = 480;
    parameter V_FRONT   = 10;
    parameter V_SYNC    = 2;
    parameter V_BACK    = 33;
    parameter V_TOTAL   = 525;

    // 計數器用reg
    reg [9:0] h_cnt = 0;
    reg [9:0] v_cnt = 0;

    // 水平計數器
    always @(posedge clk) begin
        if (h_cnt == H_TOTAL - 1)
            h_cnt <= 0;
        else
            h_cnt <= h_cnt + 1;
    end

    // 垂直計數器
    always @(posedge clk) begin
        if (h_cnt == H_TOTAL - 1) begin
            if (v_cnt == V_TOTAL - 1)
                v_cnt <= 0;
            else
                v_cnt <= v_cnt + 1;
        end
    end

    // 組合邏輯輸出
    assign hcount   = h_cnt;
    assign vcount   = v_cnt;
    assign hsync    = ~((h_cnt >= H_DISPLAY + H_FRONT) &&
                        (h_cnt <  H_DISPLAY + H_FRONT + H_SYNC));
    assign vsync    = ~((v_cnt >= V_DISPLAY + V_FRONT) &&
                        (v_cnt <  V_DISPLAY + V_FRONT + V_SYNC));
    assign video_on = (h_cnt < H_DISPLAY) && (v_cnt < V_DISPLAY);

endmodule
*/
