// Digital circuit core1.dig as structural Verilog
module core1 (
  input  clk_global,
  input  reset_global,
  input  vram_wr_gnt,
  input  [1:0] image_sel,
  output vram_req,
  output [7:0] vram_addr,
  output [2:0] vram_data
);

  wire fz, u_control_unit_rf_wr_en;
  wire [1:0] u_control_unit_rf_rd_addra, u_control_unit_rf_rd_addrb, u_control_unit_rf_wr_addr;
  wire [3:0] u_control_unit_alu_op;
  wire [7:0] result, u_control_unit_alu_op1, u_control_unit_alu_op2, u_control_unit_pc,
       u_control_unit_rf_wr_data, u_reg_file_rd_dataa, u_reg_file_rd_datab;
  wire [15:0] instr;

  control_unit #(.applicationType("IVERILOG")) u_control_unit (
    .clk(clk_global), .rst(reset_global), .instr(instr), .alu_result(result), .alu_flagZ(fz),
    .rf_dataA(u_reg_file_rd_dataa), .rf_dataB(u_reg_file_rd_datab), .vram_wr_gnt(vram_wr_gnt),
    .pc(u_control_unit_pc), .alu_op(u_control_unit_alu_op), .alu_op1(u_control_unit_alu_op1),
    .alu_op2(u_control_unit_alu_op2), .rf_rd_addrA(u_control_unit_rf_rd_addra),
    .rf_rd_addrB(u_control_unit_rf_rd_addrb), .rf_wr_en(u_control_unit_rf_wr_en),
    .rf_wr_addr(u_control_unit_rf_wr_addr), .rf_wr_data(u_control_unit_rf_wr_data), .vram_wr_req(vram_req),
    .vram_addr(vram_addr), .vram_data(vram_data));  // open: cur_opcode, cur_state
  prog_rom_c1 #(.applicationType("IVERILOG")) u_prog_rom_c1 (
    .pc(u_control_unit_pc), .img_sel(image_sel), .instr(instr));
  alu #(.applicationType("IVERILOG")) u_alu (
    .opcode(u_control_unit_alu_op), .operand1(u_control_unit_alu_op1), .operand2(u_control_unit_alu_op2),
    .result(result), .flagZ(fz));  // open: flagC
  reg_file #(.applicationType("IVERILOG")) u_reg_file (
    .clk(clk_global), .rst(reset_global), .wr_en(u_control_unit_rf_wr_en),
    .wr_addr(u_control_unit_rf_wr_addr), .wr_data(u_control_unit_rf_wr_data),
    .rd_addrA(u_control_unit_rf_rd_addra), .rd_addrB(u_control_unit_rf_rd_addrb),
    .rd_dataA(u_reg_file_rd_dataa), .rd_dataB(u_reg_file_rd_datab));

  // Other names for the same wires on the sheet: clk = clk_global; rst = reset_global; sel[1:0] = image_sel

  // Notes on the sheet:
  //   clk_global: Hz: 1000
endmodule

/* Code of control_unit:
// =================================================================
// control_unit.v  —  FSM Control Unit（16x16 版）
// =================================================================
module control_unit (
    input        clk,
    input        rst,
    output reg [7:0] pc,
    input      [15:0] instr,
    output reg [3:0] alu_op,
    output reg [7:0] alu_op1,
    output reg [7:0] alu_op2,
    input      [7:0] alu_result,
    input            alu_flagZ,
    output reg [1:0] rf_rd_addrA,
    output reg [1:0] rf_rd_addrB,
    input      [7:0] rf_dataA,
    input      [7:0] rf_dataB,
    output reg       rf_wr_en,
    output reg [1:0] rf_wr_addr,
    output reg [7:0] rf_wr_data,
    output reg       vram_wr_req,
    input            vram_wr_gnt,
    output reg [7:0] vram_addr,
    output reg [2:0] vram_data,
    output reg [3:0] cur_opcode,
    output reg [1:0] cur_state
);
    localparam [1:0] S_FETCH=2'b00, S_DECODE=2'b01, S_EXECUTE=2'b10, S_WRITEBACK=2'b11;
    localparam [3:0]
        OP_MOV=4'b0000, OP_ADD=4'b0001, OP_SUB=4'b0010,
        OP_AND=4'b0011, OP_OR =4'b0100, OP_OUT=4'b0101,
        OP_BEQ=4'b0110, OP_JMP=4'b0111;
    reg [15:0] IR;
    wire [3:0] ir_opcode = IR[15:12];
    wire [1:0] ir_rd     = IR[11:10];
    wire [1:0] ir_rs     = IR[9:8];
    wire [7:0] ir_imm8   = IR[7:0];
    reg [1:0] state;
    always @(posedge clk) begin
        if (rst) begin
            state <= S_FETCH; pc <= 8'h00;
            IR <= 16'h0000; rf_wr_en <= 0; vram_wr_req <= 0;
        end else begin
            cur_state <= state;
            case (state)
                S_FETCH: begin
                    IR <= instr; rf_wr_en <= 0; vram_wr_req <= 0;
                    state <= S_DECODE;
                end
                S_DECODE: begin
                    cur_opcode  <= ir_opcode;
                    rf_rd_addrA <= ir_rd;
                    rf_rd_addrB <= ir_rs;
                    alu_op      <= ir_opcode;
                    state       <= S_EXECUTE;
                end
                S_EXECUTE: begin
                    alu_op1 <= rf_dataA;
                    alu_op2 <= (ir_opcode==OP_MOV||ir_opcode==OP_BEQ||ir_opcode==OP_JMP)
                               ? ir_imm8 : rf_dataB;
                    if (ir_opcode == OP_OUT) begin
                        vram_addr   <= ir_imm8;
                        vram_data   <= rf_dataB[2:0];
                        vram_wr_req <= 1;
                    end
                    state <= S_WRITEBACK;
                end
                S_WRITEBACK: begin
                    vram_wr_req <= 0;
                    case (ir_opcode)
                        OP_MOV, OP_ADD, OP_SUB, OP_AND, OP_OR: begin
                            rf_wr_en <= 1; rf_wr_addr <= ir_rd;
                            rf_wr_data <= alu_result; pc <= pc + 8'h01;
                        end
                        OP_OUT: begin
                            rf_wr_en <= 0;
                            if (vram_wr_gnt) pc <= pc + 8'h01;
                            else begin vram_wr_req <= 1; state <= S_WRITEBACK; end
                        end
                        OP_BEQ: begin
                            rf_wr_en <= 0;
                            pc <= alu_flagZ ? ir_imm8 : (pc + 8'h01);
                        end
                        OP_JMP: begin rf_wr_en <= 0; pc <= ir_imm8; end
                        default: begin rf_wr_en <= 0; pc <= pc + 8'h01; end
                    endcase
                    if (ir_opcode != OP_OUT || vram_wr_gnt) state <= S_FETCH;
                end
            endcase
        end
    end
endmodule
*/

/* Code of prog_rom_c1:
// prog_rom_c1.v - Core 1: row 8~15
// key = {img_sel[1:0], pc[7:0]} = 10-bit
// 每像素2條: MOV R0,color + OUT R0->VRAM[addr]
// OUT格式: op=0101 Rd=00 Rs=00 imm8=vram_addr
//   control_unit: vram_addr=imm8, vram_data=rf_dataB(=R0)

module prog_rom_c1 (
    input  [7:0] pc,
    input  [1:0] img_sel,
    output reg [15:0] instr
);
    wire [9:0] key = {img_sel, pc};
    always @(*) begin
        case (key)
            // ==== Image 0 ====
            10'd0: instr = 16'b0000_00_00_00000000;
            10'd1: instr = 16'b0101_00_00_10000000;
            10'd2: instr = 16'b0000_00_00_00000000;
            10'd3: instr = 16'b0101_00_00_10000001;
            10'd4: instr = 16'b0000_00_00_00000000;
            10'd5: instr = 16'b0101_00_00_10000010;
            10'd6: instr = 16'b0000_00_00_00000000;
            10'd7: instr = 16'b0101_00_00_10000011;
            10'd8: instr = 16'b0000_00_00_00000000;
            10'd9: instr = 16'b0101_00_00_10000100;
            10'd10: instr = 16'b0000_00_00_00000100;
            10'd11: instr = 16'b0101_00_00_10000101;
            10'd12: instr = 16'b0000_00_00_00000000;
            10'd13: instr = 16'b0101_00_00_10000110;
            10'd14: instr = 16'b0000_00_00_00000100;
            10'd15: instr = 16'b0101_00_00_10000111;
            10'd16: instr = 16'b0000_00_00_00000000;
            10'd17: instr = 16'b0101_00_00_10001000;
            10'd18: instr = 16'b0000_00_00_00000100;
            10'd19: instr = 16'b0101_00_00_10001001;
            10'd20: instr = 16'b0000_00_00_00000000;
            10'd21: instr = 16'b0101_00_00_10001010;
            10'd22: instr = 16'b0000_00_00_00000100;
            10'd23: instr = 16'b0101_00_00_10001011;
            10'd24: instr = 16'b0000_00_00_00000000;
            10'd25: instr = 16'b0101_00_00_10001100;
            10'd26: instr = 16'b0000_00_00_00000000;
            10'd27: instr = 16'b0101_00_00_10001101;
            10'd28: instr = 16'b0000_00_00_00000000;
            10'd29: instr = 16'b0101_00_00_10001110;
            10'd30: instr = 16'b0000_00_00_00000000;
            10'd31: instr = 16'b0101_00_00_10001111;
            10'd32: instr = 16'b0000_00_00_00000000;
            10'd33: instr = 16'b0101_00_00_10010000;
            10'd34: instr = 16'b0000_00_00_00000000;
            10'd35: instr = 16'b0101_00_00_10010001;
            10'd36: instr = 16'b0000_00_00_00000000;
            10'd37: instr = 16'b0101_00_00_10010010;
            10'd38: instr = 16'b0000_00_00_00000000;
            10'd39: instr = 16'b0101_00_00_10010011;
            10'd40: instr = 16'b0000_00_00_00000000;
            10'd41: instr = 16'b0101_00_00_10010100;
            10'd42: instr = 16'b0000_00_00_00000100;
            10'd43: instr = 16'b0101_00_00_10010101;
            10'd44: instr = 16'b0000_00_00_00000000;
            10'd45: instr = 16'b0101_00_00_10010110;
            10'd46: instr = 16'b0000_00_00_00000100;
            10'd47: instr = 16'b0101_00_00_10010111;
            10'd48: instr = 16'b0000_00_00_00000000;
            10'd49: instr = 16'b0101_00_00_10011000;
            10'd50: instr = 16'b0000_00_00_00000100;
            10'd51: instr = 16'b0101_00_00_10011001;
            10'd52: instr = 16'b0000_00_00_00000000;
            10'd53: instr = 16'b0101_00_00_10011010;
            10'd54: instr = 16'b0000_00_00_00000100;
            10'd55: instr = 16'b0101_00_00_10011011;
            10'd56: instr = 16'b0000_00_00_00000000;
            10'd57: instr = 16'b0101_00_00_10011100;
            10'd58: instr = 16'b0000_00_00_00000000;
            10'd59: instr = 16'b0101_00_00_10011101;
            10'd60: instr = 16'b0000_00_00_00000000;
            10'd61: instr = 16'b0101_00_00_10011110;
            10'd62: instr = 16'b0000_00_00_00000000;
            10'd63: instr = 16'b0101_00_00_10011111;
            10'd64: instr = 16'b0000_00_00_00000000;
            10'd65: instr = 16'b0101_00_00_10100000;
            10'd66: instr = 16'b0000_00_00_00000000;
            10'd67: instr = 16'b0101_00_00_10100001;
            10'd68: instr = 16'b0000_00_00_00000000;
            10'd69: instr = 16'b0101_00_00_10100010;
            10'd70: instr = 16'b0000_00_00_00000000;
            10'd71: instr = 16'b0101_00_00_10100011;
            10'd72: instr = 16'b0000_00_00_00000100;
            10'd73: instr = 16'b0101_00_00_10100100;
            10'd74: instr = 16'b0000_00_00_00000000;
            10'd75: instr = 16'b0101_00_00_10100101;
            10'd76: instr = 16'b0000_00_00_00000100;
            10'd77: instr = 16'b0101_00_00_10100110;
            10'd78: instr = 16'b0000_00_00_00000100;
            10'd79: instr = 16'b0101_00_00_10100111;
            10'd80: instr = 16'b0000_00_00_00000000;
            10'd81: instr = 16'b0101_00_00_10101000;
            10'd82: instr = 16'b0000_00_00_00000100;
            10'd83: instr = 16'b0101_00_00_10101001;
            10'd84: instr = 16'b0000_00_00_00000100;
            10'd85: instr = 16'b0101_00_00_10101010;
            10'd86: instr = 16'b0000_00_00_00000000;
            10'd87: instr = 16'b0101_00_00_10101011;
            10'd88: instr = 16'b0000_00_00_00000100;
            10'd89: instr = 16'b0101_00_00_10101100;
            10'd90: instr = 16'b0000_00_00_00000000;
            10'd91: instr = 16'b0101_00_00_10101101;
            10'd92: instr = 16'b0000_00_00_00000000;
            10'd93: instr = 16'b0101_00_00_10101110;
            10'd94: instr = 16'b0000_00_00_00000000;
            10'd95: instr = 16'b0101_00_00_10101111;
            10'd96: instr = 16'b0000_00_00_00000000;
            10'd97: instr = 16'b0101_00_00_10110000;
            10'd98: instr = 16'b0000_00_00_00000000;
            10'd99: instr = 16'b0101_00_00_10110001;
            10'd100: instr = 16'b0000_00_00_00000000;
            10'd101: instr = 16'b0101_00_00_10110010;
            10'd102: instr = 16'b0000_00_00_00000000;
            10'd103: instr = 16'b0101_00_00_10110011;
            10'd104: instr = 16'b0000_00_00_00000000;
            10'd105: instr = 16'b0101_00_00_10110100;
            10'd106: instr = 16'b0000_00_00_00000000;
            10'd107: instr = 16'b0101_00_00_10110101;
            10'd108: instr = 16'b0000_00_00_00000000;
            10'd109: instr = 16'b0101_00_00_10110110;
            10'd110: instr = 16'b0000_00_00_00000000;
            10'd111: instr = 16'b0101_00_00_10110111;
            10'd112: instr = 16'b0000_00_00_00000000;
            10'd113: instr = 16'b0101_00_00_10111000;
            10'd114: instr = 16'b0000_00_00_00000000;
            10'd115: instr = 16'b0101_00_00_10111001;
            10'd116: instr = 16'b0000_00_00_00000000;
            10'd117: instr = 16'b0101_00_00_10111010;
            10'd118: instr = 16'b0000_00_00_00000000;
            10'd119: instr = 16'b0101_00_00_10111011;
            10'd120: instr = 16'b0000_00_00_00000000;
            10'd121: instr = 16'b0101_00_00_10111100;
            10'd122: instr = 16'b0000_00_00_00000000;
            10'd123: instr = 16'b0101_00_00_10111101;
            10'd124: instr = 16'b0000_00_00_00000000;
            10'd125: instr = 16'b0101_00_00_10111110;
            10'd126: instr = 16'b0000_00_00_00000000;
            10'd127: instr = 16'b0101_00_00_10111111;
            10'd128: instr = 16'b0000_00_00_00000000;
            10'd129: instr = 16'b0101_00_00_11000000;
            10'd130: instr = 16'b0000_00_00_00000000;
            10'd131: instr = 16'b0101_00_00_11000001;
            10'd132: instr = 16'b0000_00_00_00000000;
            10'd133: instr = 16'b0101_00_00_11000010;
            10'd134: instr = 16'b0000_00_00_00000000;
            10'd135: instr = 16'b0101_00_00_11000011;
            10'd136: instr = 16'b0000_00_00_00000111;
            10'd137: instr = 16'b0101_00_00_11000100;
            10'd138: instr = 16'b0000_00_00_00000000;
            10'd139: instr = 16'b0101_00_00_11000101;
            10'd140: instr = 16'b0000_00_00_00000000;
            10'd141: instr = 16'b0101_00_00_11000110;
            10'd142: instr = 16'b0000_00_00_00000000;
            10'd143: instr = 16'b0101_00_00_11000111;
            10'd144: instr = 16'b0000_00_00_00000000;
            10'd145: instr = 16'b0101_00_00_11001000;
            10'd146: instr = 16'b0000_00_00_00000000;
            10'd147: instr = 16'b0101_00_00_11001001;
            10'd148: instr = 16'b0000_00_00_00000000;
            10'd149: instr = 16'b0101_00_00_11001010;
            10'd150: instr = 16'b0000_00_00_00000000;
            10'd151: instr = 16'b0101_00_00_11001011;
            10'd152: instr = 16'b0000_00_00_00000000;
            10'd153: instr = 16'b0101_00_00_11001100;
            10'd154: instr = 16'b0000_00_00_00000000;
            10'd155: instr = 16'b0101_00_00_11001101;
            10'd156: instr = 16'b0000_00_00_00000000;
            10'd157: instr = 16'b0101_00_00_11001110;
            10'd158: instr = 16'b0000_00_00_00000000;
            10'd159: instr = 16'b0101_00_00_11001111;
            10'd160: instr = 16'b0000_00_00_00000000;
            10'd161: instr = 16'b0101_00_00_11010000;
            10'd162: instr = 16'b0000_00_00_00000000;
            10'd163: instr = 16'b0101_00_00_11010001;
            10'd164: instr = 16'b0000_00_00_00000000;
            10'd165: instr = 16'b0101_00_00_11010010;
            10'd166: instr = 16'b0000_00_00_00000111;
            10'd167: instr = 16'b0101_00_00_11010011;
            10'd168: instr = 16'b0000_00_00_00000000;
            10'd169: instr = 16'b0101_00_00_11010100;
            10'd170: instr = 16'b0000_00_00_00000000;
            10'd171: instr = 16'b0101_00_00_11010101;
            10'd172: instr = 16'b0000_00_00_00000000;
            10'd173: instr = 16'b0101_00_00_11010110;
            10'd174: instr = 16'b0000_00_00_00000000;
            10'd175: instr = 16'b0101_00_00_11010111;
            10'd176: instr = 16'b0000_00_00_00000000;
            10'd177: instr = 16'b0101_00_00_11011000;
            10'd178: instr = 16'b0000_00_00_00000000;
            10'd179: instr = 16'b0101_00_00_11011001;
            10'd180: instr = 16'b0000_00_00_00000000;
            10'd181: instr = 16'b0101_00_00_11011010;
            10'd182: instr = 16'b0000_00_00_00000000;
            10'd183: instr = 16'b0101_00_00_11011011;
            10'd184: instr = 16'b0000_00_00_00000000;
            10'd185: instr = 16'b0101_00_00_11011100;
            10'd186: instr = 16'b0000_00_00_00000000;
            10'd187: instr = 16'b0101_00_00_11011101;
            10'd188: instr = 16'b0000_00_00_00000000;
            10'd189: instr = 16'b0101_00_00_11011110;
            10'd190: instr = 16'b0000_00_00_00000000;
            10'd191: instr = 16'b0101_00_00_11011111;
            10'd192: instr = 16'b0000_00_00_00000000;
            10'd193: instr = 16'b0101_00_00_11100000;
            10'd194: instr = 16'b0000_00_00_00000000;
            10'd195: instr = 16'b0101_00_00_11100001;
            10'd196: instr = 16'b0000_00_00_00000111;
            10'd197: instr = 16'b0101_00_00_11100010;
            10'd198: instr = 16'b0000_00_00_00000000;
            10'd199: instr = 16'b0101_00_00_11100011;
            10'd200: instr = 16'b0000_00_00_00000000;
            10'd201: instr = 16'b0101_00_00_11100100;
            10'd202: instr = 16'b0000_00_00_00000000;
            10'd203: instr = 16'b0101_00_00_11100101;
            10'd204: instr = 16'b0000_00_00_00000000;
            10'd205: instr = 16'b0101_00_00_11100110;
            10'd206: instr = 16'b0000_00_00_00000000;
            10'd207: instr = 16'b0101_00_00_11100111;
            10'd208: instr = 16'b0000_00_00_00000000;
            10'd209: instr = 16'b0101_00_00_11101000;
            10'd210: instr = 16'b0000_00_00_00000000;
            10'd211: instr = 16'b0101_00_00_11101001;
            10'd212: instr = 16'b0000_00_00_00000000;
            10'd213: instr = 16'b0101_00_00_11101010;
            10'd214: instr = 16'b0000_00_00_00000000;
            10'd215: instr = 16'b0101_00_00_11101011;
            10'd216: instr = 16'b0000_00_00_00000000;
            10'd217: instr = 16'b0101_00_00_11101100;
            10'd218: instr = 16'b0000_00_00_00000000;
            10'd219: instr = 16'b0101_00_00_11101101;
            10'd220: instr = 16'b0000_00_00_00000000;
            10'd221: instr = 16'b0101_00_00_11101110;
            10'd222: instr = 16'b0000_00_00_00000000;
            10'd223: instr = 16'b0101_00_00_11101111;
            10'd224: instr = 16'b0000_00_00_00000000;
            10'd225: instr = 16'b0101_00_00_11110000;
            10'd226: instr = 16'b0000_00_00_00000000;
            10'd227: instr = 16'b0101_00_00_11110001;
            10'd228: instr = 16'b0000_00_00_00000000;
            10'd229: instr = 16'b0101_00_00_11110010;
            10'd230: instr = 16'b0000_00_00_00000000;
            10'd231: instr = 16'b0101_00_00_11110011;
            10'd232: instr = 16'b0000_00_00_00000000;
            10'd233: instr = 16'b0101_00_00_11110100;
            10'd234: instr = 16'b0000_00_00_00000000;
            10'd235: instr = 16'b0101_00_00_11110101;
            10'd236: instr = 16'b0000_00_00_00000000;
            10'd237: instr = 16'b0101_00_00_11110110;
            10'd238: instr = 16'b0000_00_00_00000000;
            10'd239: instr = 16'b0101_00_00_11110111;
            10'd240: instr = 16'b0000_00_00_00000000;
            10'd241: instr = 16'b0101_00_00_11111000;
            10'd242: instr = 16'b0000_00_00_00000000;
            10'd243: instr = 16'b0101_00_00_11111001;
            10'd244: instr = 16'b0000_00_00_00000000;
            10'd245: instr = 16'b0101_00_00_11111010;
            10'd246: instr = 16'b0000_00_00_00000000;
            10'd247: instr = 16'b0101_00_00_11111011;
            10'd248: instr = 16'b0000_00_00_00000000;
            10'd249: instr = 16'b0101_00_00_11111100;
            10'd250: instr = 16'b0000_00_00_00000000;
            10'd251: instr = 16'b0101_00_00_11111101;
            10'd252: instr = 16'b0000_00_00_00000000;
            10'd253: instr = 16'b0101_00_00_11111110;
            10'd254: instr = 16'b0000_00_00_00000000;
            10'd255: instr = 16'b0101_00_00_11111111;
            // ==== Image 1 ====
            10'd256: instr = 16'b0000_00_00_00000000;
            10'd257: instr = 16'b0101_00_00_10000000;
            10'd258: instr = 16'b0000_00_00_00000000;
            10'd259: instr = 16'b0101_00_00_10000001;
            10'd260: instr = 16'b0000_00_00_00000000;
            10'd261: instr = 16'b0101_00_00_10000010;
            10'd262: instr = 16'b0000_00_00_00000000;
            10'd263: instr = 16'b0101_00_00_10000011;
            10'd264: instr = 16'b0000_00_00_00000110;
            10'd265: instr = 16'b0101_00_00_10000100;
            10'd266: instr = 16'b0000_00_00_00000110;
            10'd267: instr = 16'b0101_00_00_10000101;
            10'd268: instr = 16'b0000_00_00_00000110;
            10'd269: instr = 16'b0101_00_00_10000110;
            10'd270: instr = 16'b0000_00_00_00000110;
            10'd271: instr = 16'b0101_00_00_10000111;
            10'd272: instr = 16'b0000_00_00_00000000;
            10'd273: instr = 16'b0101_00_00_10001000;
            10'd274: instr = 16'b0000_00_00_00000000;
            10'd275: instr = 16'b0101_00_00_10001001;
            10'd276: instr = 16'b0000_00_00_00000000;
            10'd277: instr = 16'b0101_00_00_10001010;
            10'd278: instr = 16'b0000_00_00_00000000;
            10'd279: instr = 16'b0101_00_00_10001011;
            10'd280: instr = 16'b0000_00_00_00000000;
            10'd281: instr = 16'b0101_00_00_10001100;
            10'd282: instr = 16'b0000_00_00_00000000;
            10'd283: instr = 16'b0101_00_00_10001101;
            10'd284: instr = 16'b0000_00_00_00000000;
            10'd285: instr = 16'b0101_00_00_10001110;
            10'd286: instr = 16'b0000_00_00_00000000;
            10'd287: instr = 16'b0101_00_00_10001111;
            10'd288: instr = 16'b0000_00_00_00000000;
            10'd289: instr = 16'b0101_00_00_10010000;
            10'd290: instr = 16'b0000_00_00_00000000;
            10'd291: instr = 16'b0101_00_00_10010001;
            10'd292: instr = 16'b0000_00_00_00000000;
            10'd293: instr = 16'b0101_00_00_10010010;
            10'd294: instr = 16'b0000_00_00_00000000;
            10'd295: instr = 16'b0101_00_00_10010011;
            10'd296: instr = 16'b0000_00_00_00000110;
            10'd297: instr = 16'b0101_00_00_10010100;
            10'd298: instr = 16'b0000_00_00_00000110;
            10'd299: instr = 16'b0101_00_00_10010101;
            10'd300: instr = 16'b0000_00_00_00000110;
            10'd301: instr = 16'b0101_00_00_10010110;
            10'd302: instr = 16'b0000_00_00_00000110;
            10'd303: instr = 16'b0101_00_00_10010111;
            10'd304: instr = 16'b0000_00_00_00000110;
            10'd305: instr = 16'b0101_00_00_10011000;
            10'd306: instr = 16'b0000_00_00_00000110;
            10'd307: instr = 16'b0101_00_00_10011001;
            10'd308: instr = 16'b0000_00_00_00000000;
            10'd309: instr = 16'b0101_00_00_10011010;
            10'd310: instr = 16'b0000_00_00_00000000;
            10'd311: instr = 16'b0101_00_00_10011011;
            10'd312: instr = 16'b0000_00_00_00000000;
            10'd313: instr = 16'b0101_00_00_10011100;
            10'd314: instr = 16'b0000_00_00_00000000;
            10'd315: instr = 16'b0101_00_00_10011101;
            10'd316: instr = 16'b0000_00_00_00000000;
            10'd317: instr = 16'b0101_00_00_10011110;
            10'd318: instr = 16'b0000_00_00_00000000;
            10'd319: instr = 16'b0101_00_00_10011111;
            10'd320: instr = 16'b0000_00_00_00000000;
            10'd321: instr = 16'b0101_00_00_10100000;
            10'd322: instr = 16'b0000_00_00_00000000;
            10'd323: instr = 16'b0101_00_00_10100001;
            10'd324: instr = 16'b0000_00_00_00000000;
            10'd325: instr = 16'b0101_00_00_10100010;
            10'd326: instr = 16'b0000_00_00_00000000;
            10'd327: instr = 16'b0101_00_00_10100011;
            10'd328: instr = 16'b0000_00_00_00000110;
            10'd329: instr = 16'b0101_00_00_10100100;
            10'd330: instr = 16'b0000_00_00_00000110;
            10'd331: instr = 16'b0101_00_00_10100101;
            10'd332: instr = 16'b0000_00_00_00000110;
            10'd333: instr = 16'b0101_00_00_10100110;
            10'd334: instr = 16'b0000_00_00_00000110;
            10'd335: instr = 16'b0101_00_00_10100111;
            10'd336: instr = 16'b0000_00_00_00000110;
            10'd337: instr = 16'b0101_00_00_10101000;
            10'd338: instr = 16'b0000_00_00_00000110;
            10'd339: instr = 16'b0101_00_00_10101001;
            10'd340: instr = 16'b0000_00_00_00000110;
            10'd341: instr = 16'b0101_00_00_10101010;
            10'd342: instr = 16'b0000_00_00_00000000;
            10'd343: instr = 16'b0101_00_00_10101011;
            10'd344: instr = 16'b0000_00_00_00000000;
            10'd345: instr = 16'b0101_00_00_10101100;
            10'd346: instr = 16'b0000_00_00_00000000;
            10'd347: instr = 16'b0101_00_00_10101101;
            10'd348: instr = 16'b0000_00_00_00000000;
            10'd349: instr = 16'b0101_00_00_10101110;
            10'd350: instr = 16'b0000_00_00_00000000;
            10'd351: instr = 16'b0101_00_00_10101111;
            10'd352: instr = 16'b0000_00_00_00000000;
            10'd353: instr = 16'b0101_00_00_10110000;
            10'd354: instr = 16'b0000_00_00_00000000;
            10'd355: instr = 16'b0101_00_00_10110001;
            10'd356: instr = 16'b0000_00_00_00000000;
            10'd357: instr = 16'b0101_00_00_10110010;
            10'd358: instr = 16'b0000_00_00_00000000;
            10'd359: instr = 16'b0101_00_00_10110011;
            10'd360: instr = 16'b0000_00_00_00000000;
            10'd361: instr = 16'b0101_00_00_10110100;
            10'd362: instr = 16'b0000_00_00_00000110;
            10'd363: instr = 16'b0101_00_00_10110101;
            10'd364: instr = 16'b0000_00_00_00000110;
            10'd365: instr = 16'b0101_00_00_10110110;
            10'd366: instr = 16'b0000_00_00_00000110;
            10'd367: instr = 16'b0101_00_00_10110111;
            10'd368: instr = 16'b0000_00_00_00000110;
            10'd369: instr = 16'b0101_00_00_10111000;
            10'd370: instr = 16'b0000_00_00_00000110;
            10'd371: instr = 16'b0101_00_00_10111001;
            10'd372: instr = 16'b0000_00_00_00000110;
            10'd373: instr = 16'b0101_00_00_10111010;
            10'd374: instr = 16'b0000_00_00_00000110;
            10'd375: instr = 16'b0101_00_00_10111011;
            10'd376: instr = 16'b0000_00_00_00000000;
            10'd377: instr = 16'b0101_00_00_10111100;
            10'd378: instr = 16'b0000_00_00_00000000;
            10'd379: instr = 16'b0101_00_00_10111101;
            10'd380: instr = 16'b0000_00_00_00000000;
            10'd381: instr = 16'b0101_00_00_10111110;
            10'd382: instr = 16'b0000_00_00_00000000;
            10'd383: instr = 16'b0101_00_00_10111111;
            10'd384: instr = 16'b0000_00_00_00000000;
            10'd385: instr = 16'b0101_00_00_11000000;
            10'd386: instr = 16'b0000_00_00_00000000;
            10'd387: instr = 16'b0101_00_00_11000001;
            10'd388: instr = 16'b0000_00_00_00000000;
            10'd389: instr = 16'b0101_00_00_11000010;
            10'd390: instr = 16'b0000_00_00_00000000;
            10'd391: instr = 16'b0101_00_00_11000011;
            10'd392: instr = 16'b0000_00_00_00000000;
            10'd393: instr = 16'b0101_00_00_11000100;
            10'd394: instr = 16'b0000_00_00_00000110;
            10'd395: instr = 16'b0101_00_00_11000101;
            10'd396: instr = 16'b0000_00_00_00000110;
            10'd397: instr = 16'b0101_00_00_11000110;
            10'd398: instr = 16'b0000_00_00_00000110;
            10'd399: instr = 16'b0101_00_00_11000111;
            10'd400: instr = 16'b0000_00_00_00000110;
            10'd401: instr = 16'b0101_00_00_11001000;
            10'd402: instr = 16'b0000_00_00_00000110;
            10'd403: instr = 16'b0101_00_00_11001001;
            10'd404: instr = 16'b0000_00_00_00000110;
            10'd405: instr = 16'b0101_00_00_11001010;
            10'd406: instr = 16'b0000_00_00_00000110;
            10'd407: instr = 16'b0101_00_00_11001011;
            10'd408: instr = 16'b0000_00_00_00000000;
            10'd409: instr = 16'b0101_00_00_11001100;
            10'd410: instr = 16'b0000_00_00_00000000;
            10'd411: instr = 16'b0101_00_00_11001101;
            10'd412: instr = 16'b0000_00_00_00000000;
            10'd413: instr = 16'b0101_00_00_11001110;
            10'd414: instr = 16'b0000_00_00_00000000;
            10'd415: instr = 16'b0101_00_00_11001111;
            10'd416: instr = 16'b0000_00_00_00000000;
            10'd417: instr = 16'b0101_00_00_11010000;
            10'd418: instr = 16'b0000_00_00_00000000;
            10'd419: instr = 16'b0101_00_00_11010001;
            10'd420: instr = 16'b0000_00_00_00000000;
            10'd421: instr = 16'b0101_00_00_11010010;
            10'd422: instr = 16'b0000_00_00_00000000;
            10'd423: instr = 16'b0101_00_00_11010011;
            10'd424: instr = 16'b0000_00_00_00000000;
            10'd425: instr = 16'b0101_00_00_11010100;
            10'd426: instr = 16'b0000_00_00_00000000;
            10'd427: instr = 16'b0101_00_00_11010101;
            10'd428: instr = 16'b0000_00_00_00000110;
            10'd429: instr = 16'b0101_00_00_11010110;
            10'd430: instr = 16'b0000_00_00_00000110;
            10'd431: instr = 16'b0101_00_00_11010111;
            10'd432: instr = 16'b0000_00_00_00000110;
            10'd433: instr = 16'b0101_00_00_11011000;
            10'd434: instr = 16'b0000_00_00_00000110;
            10'd435: instr = 16'b0101_00_00_11011001;
            10'd436: instr = 16'b0000_00_00_00000110;
            10'd437: instr = 16'b0101_00_00_11011010;
            10'd438: instr = 16'b0000_00_00_00000000;
            10'd439: instr = 16'b0101_00_00_11011011;
            10'd440: instr = 16'b0000_00_00_00000000;
            10'd441: instr = 16'b0101_00_00_11011100;
            10'd442: instr = 16'b0000_00_00_00000000;
            10'd443: instr = 16'b0101_00_00_11011101;
            10'd444: instr = 16'b0000_00_00_00000000;
            10'd445: instr = 16'b0101_00_00_11011110;
            10'd446: instr = 16'b0000_00_00_00000000;
            10'd447: instr = 16'b0101_00_00_11011111;
            10'd448: instr = 16'b0000_00_00_00000000;
            10'd449: instr = 16'b0101_00_00_11100000;
            10'd450: instr = 16'b0000_00_00_00000000;
            10'd451: instr = 16'b0101_00_00_11100001;
            10'd452: instr = 16'b0000_00_00_00000000;
            10'd453: instr = 16'b0101_00_00_11100010;
            10'd454: instr = 16'b0000_00_00_00000000;
            10'd455: instr = 16'b0101_00_00_11100011;
            10'd456: instr = 16'b0000_00_00_00000000;
            10'd457: instr = 16'b0101_00_00_11100100;
            10'd458: instr = 16'b0000_00_00_00000000;
            10'd459: instr = 16'b0101_00_00_11100101;
            10'd460: instr = 16'b0000_00_00_00000000;
            10'd461: instr = 16'b0101_00_00_11100110;
            10'd462: instr = 16'b0000_00_00_00000000;
            10'd463: instr = 16'b0101_00_00_11100111;
            10'd464: instr = 16'b0000_00_00_00000000;
            10'd465: instr = 16'b0101_00_00_11101000;
            10'd466: instr = 16'b0000_00_00_00000000;
            10'd467: instr = 16'b0101_00_00_11101001;
            10'd468: instr = 16'b0000_00_00_00000000;
            10'd469: instr = 16'b0101_00_00_11101010;
            10'd470: instr = 16'b0000_00_00_00000000;
            10'd471: instr = 16'b0101_00_00_11101011;
            10'd472: instr = 16'b0000_00_00_00000000;
            10'd473: instr = 16'b0101_00_00_11101100;
            10'd474: instr = 16'b0000_00_00_00000000;
            10'd475: instr = 16'b0101_00_00_11101101;
            10'd476: instr = 16'b0000_00_00_00000000;
            10'd477: instr = 16'b0101_00_00_11101110;
            10'd478: instr = 16'b0000_00_00_00000000;
            10'd479: instr = 16'b0101_00_00_11101111;
            10'd480: instr = 16'b0000_00_00_00000000;
            10'd481: instr = 16'b0101_00_00_11110000;
            10'd482: instr = 16'b0000_00_00_00000000;
            10'd483: instr = 16'b0101_00_00_11110001;
            10'd484: instr = 16'b0000_00_00_00000000;
            10'd485: instr = 16'b0101_00_00_11110010;
            10'd486: instr = 16'b0000_00_00_00000000;
            10'd487: instr = 16'b0101_00_00_11110011;
            10'd488: instr = 16'b0000_00_00_00000000;
            10'd489: instr = 16'b0101_00_00_11110100;
            10'd490: instr = 16'b0000_00_00_00000000;
            10'd491: instr = 16'b0101_00_00_11110101;
            10'd492: instr = 16'b0000_00_00_00000000;
            10'd493: instr = 16'b0101_00_00_11110110;
            10'd494: instr = 16'b0000_00_00_00000000;
            10'd495: instr = 16'b0101_00_00_11110111;
            10'd496: instr = 16'b0000_00_00_00000000;
            10'd497: instr = 16'b0101_00_00_11111000;
            10'd498: instr = 16'b0000_00_00_00000000;
            10'd499: instr = 16'b0101_00_00_11111001;
            10'd500: instr = 16'b0000_00_00_00000000;
            10'd501: instr = 16'b0101_00_00_11111010;
            10'd502: instr = 16'b0000_00_00_00000000;
            10'd503: instr = 16'b0101_00_00_11111011;
            10'd504: instr = 16'b0000_00_00_00000000;
            10'd505: instr = 16'b0101_00_00_11111100;
            10'd506: instr = 16'b0000_00_00_00000000;
            10'd507: instr = 16'b0101_00_00_11111101;
            10'd508: instr = 16'b0000_00_00_00000000;
            10'd509: instr = 16'b0101_00_00_11111110;
            10'd510: instr = 16'b0000_00_00_00000000;
            10'd511: instr = 16'b0101_00_00_11111111;
            // ==== Image 2 ====
            10'd512: instr = 16'b0000_00_00_00000111;
            10'd513: instr = 16'b0101_00_00_10000000;
            10'd514: instr = 16'b0000_00_00_00000001;
            10'd515: instr = 16'b0101_00_00_10000001;
            10'd516: instr = 16'b0000_00_00_00000100;
            10'd517: instr = 16'b0101_00_00_10000010;
            10'd518: instr = 16'b0000_00_00_00000000;
            10'd519: instr = 16'b0101_00_00_10000011;
            10'd520: instr = 16'b0000_00_00_00000000;
            10'd521: instr = 16'b0101_00_00_10000100;
            10'd522: instr = 16'b0000_00_00_00000100;
            10'd523: instr = 16'b0101_00_00_10000101;
            10'd524: instr = 16'b0000_00_00_00000100;
            10'd525: instr = 16'b0101_00_00_10000110;
            10'd526: instr = 16'b0000_00_00_00000100;
            10'd527: instr = 16'b0101_00_00_10000111;
            10'd528: instr = 16'b0000_00_00_00000100;
            10'd529: instr = 16'b0101_00_00_10001000;
            10'd530: instr = 16'b0000_00_00_00000100;
            10'd531: instr = 16'b0101_00_00_10001001;
            10'd532: instr = 16'b0000_00_00_00000100;
            10'd533: instr = 16'b0101_00_00_10001010;
            10'd534: instr = 16'b0000_00_00_00000100;
            10'd535: instr = 16'b0101_00_00_10001011;
            10'd536: instr = 16'b0000_00_00_00000100;
            10'd537: instr = 16'b0101_00_00_10001100;
            10'd538: instr = 16'b0000_00_00_00000000;
            10'd539: instr = 16'b0101_00_00_10001101;
            10'd540: instr = 16'b0000_00_00_00000111;
            10'd541: instr = 16'b0101_00_00_10001110;
            10'd542: instr = 16'b0000_00_00_00000000;
            10'd543: instr = 16'b0101_00_00_10001111;
            10'd544: instr = 16'b0000_00_00_00000001;
            10'd545: instr = 16'b0101_00_00_10010000;
            10'd546: instr = 16'b0000_00_00_00000001;
            10'd547: instr = 16'b0101_00_00_10010001;
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*/

/* Code of alu:
// =================================================================
// alu.v  —  8-bit ALU for Dual-Core CPU
//
// ISA opcodes (4-bit):
//   0000  MOV  : Result = Operand2 (immediate passthrough)
//   0001  ADD  : Result = Op1 + Op2
//   0010  SUB  : Result = Op1 - Op2
//   0011  AND  : Result = Op1 & Op2
//   0100  OR   : Result = Op1 | Op2
//   0101  OUT  : Result = Op2 (pixel color passthrough → VRAM)
//   0110  BEQ  : Result = Op1 (branch決定由control unit看flagZ)
//   0111  JMP  : Result = Op2 (target addr passthrough)
//
// flagZ : Result == 0  (BEQ 用)
// flagC : carry out    (備用，可接七段顯示)
// =================================================================

module alu (
    input  [3:0] opcode,
    input  [7:0] operand1,   // Rs (source register value)
    input  [7:0] operand2,   // Rd or immediate
    output reg [7:0] result,
    output reg flagZ,
    output reg flagC
);

    // ----------------------------------------------------------
    // Opcode parameters (與 control_unit.v 共用，建議未來改成
    // `include "isa_def.vh"，這裡先用 localparam 定義清楚)
    // ----------------------------------------------------------
    localparam [3:0]
        OP_MOV = 4'b0000,
        OP_ADD = 4'b0001,
        OP_SUB = 4'b0010,
        OP_AND = 4'b0011,
        OP_OR  = 4'b0100,
        OP_OUT = 4'b0101,   // 畫像素：把 operand2 (顏色) 直接輸出
        OP_BEQ = 4'b0110,   // branch if zero：ALU 只做 pass，PC 由 CU 控制
        OP_JMP = 4'b0111;   // jump：ALU pass target，CU 接手

    // ----------------------------------------------------------
    // 9-bit 暫存：[8] 存 carry，[7:0] 存結果
    // （參考作業寫法：用更寬的暫存截取進位）
    // ----------------------------------------------------------
    reg [8:0] tmp;

    always @(*) begin
        // 預設值（避免 latch）
        tmp   = 9'b0;
        flagC = 1'b0;
        flagZ = 1'b0;

        case (opcode)

            // --------------------------------------------------
            // MOV Rd, imm  →  Rd ← imm（operand2 是 immediate）
            // --------------------------------------------------
            OP_MOV: begin
                tmp   = {1'b0, operand2};
                flagC = 1'b0;
            end

            // --------------------------------------------------
            // ADD Rd, Rs  →  Rd ← Rd + Rs
            // --------------------------------------------------
            OP_ADD: begin
                tmp   = {1'b0, operand1} + {1'b0, operand2};
                flagC = tmp[8];              // 與作業相同：bit[8] 當 carry
            end

            // --------------------------------------------------
            // SUB Rd, Rs  →  Rd ← Rd - Rs
            // --------------------------------------------------
            OP_SUB: begin
                tmp   = {1'b0, operand1} - {1'b0, operand2};
                flagC = tmp[8];              // borrow flag（同作業 SUB 處理）
            end

            // --------------------------------------------------
            // AND Rd, Rs  →  Rd ← Rd & Rs
            // --------------------------------------------------
            OP_AND: begin
                tmp   = {1'b0, operand1 & operand2};
                flagC = 1'b0;               // 邏輯運算不影響 carry（同作業）
            end

            // --------------------------------------------------
            // OR Rd, Rs  →  Rd ← Rd | Rs
            // --------------------------------------------------
            OP_OR: begin
                tmp   = {1'b0, operand1 | operand2};
                flagC = 1'b0;
            end

            // --------------------------------------------------
            // OUT addr, Rs  →  把 Rs 的 RGB 值輸出（pass-through）
            // ALU 只負責把 operand1（Rs 的顏色值）傳遞出去
            // control_unit 負責把 result 寫入 VRAM
            // --------------------------------------------------
            OP_OUT: begin
                tmp   = {1'b0, operand1};   // operand1 = Rs (pixel color)
                flagC = 1'b0;
            end

            // --------------------------------------------------
            // BEQ Rs, imm  →  if Rs == 0: PC ← imm
            // ALU 傳出 Rs 的值讓 CU 檢查 flagZ；
            // target address 另由指令 immediate 欄位提供
            // --------------------------------------------------
            OP_BEQ: begin
                tmp   = {1'b0, operand1};   // operand1 = Rs（讓 flagZ 反映是否為 0）
                flagC = 1'b0;
            end

            // --------------------------------------------------
            // JMP imm  →  PC ← imm（無條件跳轉）
            // ALU 傳遞 target（operand2），CU 直接載入 PC
            // --------------------------------------------------
            OP_JMP: begin
                tmp   = {1'b0, operand2};   // operand2 = immediate target
                flagC = 1'b0;
            end

            // --------------------------------------------------
            // Default：輸出 0，旗標清零
            // --------------------------------------------------
            default: begin
                tmp   = 9'b0;
                flagC = 1'b0;
            end

        endcase

        // flagZ：result[7:0] 全為 0 時拉高（同作業邏輯，但改成 8-bit 判斷）
        result = tmp[7:0];
        flagZ  = (result == 8'h00);
    end

endmodule
*/

/* Code of reg_file:
// =================================================================
// reg_file.v  —  Register File for Dual-Core CPU
//
// 4 個 8-bit 暫存器 R0–R3
// 2 個非同步讀取 port（combinational）
// 1 個同步寫入 port（posedge clk，有 wr_en 控制）
// rst 高電位同步清零
// =================================================================

module reg_file (
    input            clk,
    input            rst,
    // 寫入 port
    input            wr_en,
    input      [1:0] wr_addr,   // R0=00, R1=01, R2=10, R3=11
    input      [7:0] wr_data,
    // 讀取 port A（Rd / operand1）
    input      [1:0] rd_addrA,
    output     [7:0] rd_dataA,
    // 讀取 port B（Rs / operand2）
    input      [1:0] rd_addrB,
    output     [7:0] rd_dataB
);

    reg [7:0] regs [0:3];   // R0, R1, R2, R3

    // 同步寫入
    integer i;
    always @(posedge clk) begin
        if (rst) begin
            regs[0] <= 8'h00;
            regs[1] <= 8'h00;
            regs[2] <= 8'h00;
            regs[3] <= 8'h00;
        end else if (wr_en) begin
            regs[wr_addr] <= wr_data;
        end
    end

    // 非同步讀取（combinational）
    assign rd_dataA = regs[rd_addrA];
    assign rd_dataB = regs[rd_addrB];

endmodule
*/
