// Digital circuit dual.dig as structural Verilog
module dual (
  input  clk_global,
  input  reset_global,
  input  [1:0] image_sel
);

  wire gnt0, gnt1, hsync, req0, req1, u_pixel_driver_b, u_pixel_driver_g, u_pixel_driver_r, video_on, vsync;
  wire [2:0] u_vram_rd_data, vram_data0, vram_data1;
  wire [7:0] u_pixel_driver_vram_rd_addr, vram_addr0, vram_addr1;
  wire [9:0] hcount, vcount;

  bus_arbiter #(.applicationType("IVERILOG")) u_bus_arbiter (
    .clk(clk_global), .rst(reset_global), .req0(req0), .req1(req1), .gnt0(gnt0), .gnt1(gnt1));
  // core0 core0_1: pin names not known; wires that end beside it: clk_global, reset_global, image_sel, gnt0
  // core1 core1_1: pin names not known; wires that end beside it: clk_global, reset_global, image_sel, gnt1
  // VGA vga_1: pin names not known; wires that end beside it: clk_global, hsync, vsync, video_on, hcount, vcount
  vram #(.applicationType("IVERILOG")) u_vram (
    .clk(clk_global), .wr_en0(gnt0), .wr_addr0(vram_addr0), .wr_data0(vram_data0), .wr_en1(gnt1),
    .wr_addr1(vram_addr1), .wr_data1(vram_data1), .rd_addr(u_pixel_driver_vram_rd_addr),
    .rd_data(u_vram_rd_data));
  pixel_driver #(.applicationType("IVERILOG")) u_pixel_driver (
    .clk(clk_global), .rst(reset_global), .hcount(hcount), .vcount(vcount), .video_on(video_on),
    .vram_rd_data(u_vram_rd_data), .vram_rd_addr(u_pixel_driver_vram_rd_addr), .R(u_pixel_driver_r),
    .G(u_pixel_driver_g), .B(u_pixel_driver_b));
  VGA vga_2 (.R(u_pixel_driver_r), .G(u_pixel_driver_g), .B(u_pixel_driver_b), .H(hsync), .V(vsync), .C(clk_global));

  // Other names for the same wires on the sheet: clk = clk_global; rst = reset_global; sel[1:0] = image_sel

  // Notes on the sheet:
  //   clk_global: Hz: 2147483647
endmodule

/* Code of bus_arbiter:
// =================================================================
// bus_arbiter.v  —  Round-Robin Bus Arbiter
//
// 兩個 core 競爭 VRAM 寫入權
// 策略：round-robin，誰先請求就先給，平手時交替
// gnt 只在 req 有效時拉高，且一次只給一個
// =================================================================

module bus_arbiter (
    input  clk,
    input  rst,

    // Core 0
    input  req0,
    output reg gnt0,

    // Core 1
    input  req1,
    output reg gnt1
);

    reg last_gnt;   // 0 = 上次給 core0，1 = 上次給 core1

    always @(posedge clk) begin
        if (rst) begin
            gnt0     <= 1'b0;
            gnt1     <= 1'b0;
            last_gnt <= 1'b0;
        end else begin
            gnt0 <= 1'b0;
            gnt1 <= 1'b0;

            if (req0 && req1) begin
                // 雙方同時請求 → 輪流
                if (last_gnt == 1'b0) begin
                    gnt1     <= 1'b1;
                    last_gnt <= 1'b1;
                end else begin
                    gnt0     <= 1'b1;
                    last_gnt <= 1'b0;
                end
            end else if (req0) begin
                gnt0     <= 1'b1;
                last_gnt <= 1'b0;
            end else if (req1) begin
                gnt1     <= 1'b1;
                last_gnt <= 1'b1;
            end
        end
    end

endmodule
*/

/* Code of vram:
// =================================================================
// vram.v  —  Shared VRAM  256 × 3-bit（16×16 像素）
//
// addr 0~127   → Core 0（row 0~7）
// addr 128~255 → Core 1（row 8~15）
// =================================================================

module vram (
    input        clk,
    input        wr_en0,
    input  [7:0] wr_addr0,
    input  [2:0] wr_data0,
    input        wr_en1,
    input  [7:0] wr_addr1,
    input  [2:0] wr_data1,
    input  [7:0] rd_addr,
    output [2:0] rd_data
);
    reg [2:0] mem [0:255];

    always @(posedge clk) begin
        if (wr_en0) mem[wr_addr0] <= wr_data0;
        if (wr_en1) mem[wr_addr1] <= wr_data1;
    end

    assign rd_data = mem[rd_addr];
endmodule
*/

/* Code of pixel_driver:
// =================================================================
// pixel_driver.v  —  VGA 640×480 版（16×16 VRAM 放大顯示）
//
// 16×16 VRAM 放大到 640×480：
//   每個像素放大成 40×30 個 VGA 像素
//   hcount / 40 = vram_x (0~15)
//   vcount / 30 = vram_y (0~15)
//   vram_addr   = vram_y * 16 + vram_x (0~255)
// =================================================================
module pixel_driver (
    input        clk,
    input        rst,
    // 來自 vga_sync（640×480）
    input  [9:0] hcount,
    input  [9:0] vcount,
    input        video_on,
    // VRAM 讀取介面
    output [7:0] vram_rd_addr,
    input  [2:0] vram_rd_data,   // [2]=R [1]=G [0]=B
    // VGA RGB 輸出（1-bit each）
    output R,
    output G,
    output B
);
    // 用查找表做除法（避免模擬器不支援除法運算子）
    // hcount 0~639  / 40 → 0~15
    // vcount 0~479  / 30 → 0~15
    reg [3:0] hmap [0:639];
    reg [3:0] vmap [0:479];
    integer i;
    initial begin
        for (i = 0; i < 640; i = i + 1)
            hmap[i] = i / 40;
        for (i = 0; i < 480; i = i + 1)
            vmap[i] = i / 30;
    end

    wire [3:0] px = hmap[hcount];
    wire [3:0] py = vmap[vcount];

    // VRAM 位址 = py * 16 + px
    assign vram_rd_addr = {py, px};

    // RGB 輸出
    assign R = video_on ? vram_rd_data[2] : 1'b0;
    assign G = video_on ? vram_rd_data[1] : 1'b0;
    assign B = video_on ? vram_rd_data[0] : 1'b0;
endmodule
*/
