// Digital circuit Q2.dig as structural Verilog
module Q2 (
  input  A,
  input  B,
  input  C,
  input  D,
  output E
);

  wire not_1_out, not_2_out, not_3_out, not_4_out, xor_1_out, xor_2_out;

  not not_1 (not_1_out, A);
  not not_2 (not_2_out, B);
  not not_3 (not_3_out, C);
  not not_4 (not_4_out, D);
  xor xor_1 (xor_1_out, A, B);
  xor xor_2 (xor_2_out, xor_1_out, C);
  xor xor_3 (E, xor_2_out, D);
endmodule
