// Digital circuit bcd.dig as structural Verilog
module bcd (
  input  CLK,
  input  X,
  output Z,
  output [1:0] S
);

  BCD_Detector #(.applicationType("GHDL"), .Code_File("C:\\Users\\User-010855\\Desktop\\lab10\\BCDEC.vhdl")) u_BCD_Detector (
    .clk(CLK), .X(X), .Z(Z), .state_bits(S));
endmodule

/* Code of BCD_Detector:
library IEEE;
use IEEE.STD_LOGIC_1164.ALL;
use IEEE.STD_LOGIC_UNSIGNED.ALL;

entity BCD_Detector is
    Port ( 
        clk        : in  STD_LOGIC;
        X          : in  STD_LOGIC;                    -- 修改：改回 1-bit 序列輸入
        Z          : out STD_LOGIC;
        state_bits : out STD_LOGIC_VECTOR(1 downto 0)  -- 保持：2-bit 狀態編碼輸出
    );
end BCD_Detector;

architecture Behavioral of BCD_Detector is
    type state_type is (S0, S1, S2, S3);
    signal current_state : state_type := S0;
    signal next_state    : state_type;
    
    -- 新增：用來依序儲存前 3 個輸入 bit 的內部暫存器
    signal temp_reg      : STD_LOGIC_VECTOR(2 downto 0) := "000";
    -- 新增：用來把前 3 個 bit 與目前的第 4 個 bit (X) 拼成 4-bit 向量
    signal full_vector   : STD_LOGIC_VECTOR(3 downto 0);
begin

    -- 同步邏輯：負責狀態轉換，以及在每個時脈正緣把輸入的 1-bit X 存下來
    process(clk)
    begin
        if rising_edge(clk) then
            current_state <= next_state;
            
            -- 依據當前狀態，把輸入的 1-bit 依序存入 temp_reg
            case current_state is
                when S0 =>
                    temp_reg(2) <= X; -- 存下第 1 個輸入的 bit
                when S1 =>
                    temp_reg(1) <= X; -- 存下第 2 個輸入的 bit
                when S2 =>
                    temp_reg(0) <= X; -- 存下第 3 個輸入的 bit
                when others =>
                    null;             -- S3 時不需要再存，因為第 4 個 bit 直接由當前的 X 參與判斷
            end case;
        end if;
    end process;


    -- =================【注意：輸入順序設定】=================
    -- 預設以下為「MSB 高位元先輸入」的拼法（最常見）：
    full_vector <= temp_reg(2) & temp_reg(1) & temp_reg(0) & X;
    
    -- 備註：如果你們實驗講義或老師規定是「LSB 低位元先輸入」，請把上面這行改成：
    -- full_vector <= X & temp_reg(2) & temp_reg(1) & temp_reg(0);
    -- =======================================================


    -- 組合邏輯：決定下一個狀態、輸出 Z、以及狀態燈號 state_bits
    process(current_state, X, full_vector)
    begin
        -- 賦予預設值，防止電路產生不必要的 Latch (鎖存器)
        Z          <= '0';
        next_state <= current_state;
        state_bits <= "00";

        case current_state is
            when S0 =>
                next_state <= S1;
                state_bits <= "00";

            when S1 =>
                next_state <= S2;
                state_bits <= "01";

            when S2 =>
                next_state <= S3;
                state_bits <= "10";

            when S3 =>
                next_state <= S0; -- 第 4 次觸發後，自動回到 S0 循環重置
                state_bits <= "11";
                
                -- 在第 4 個狀態（S3）且收到最後一個 bit 的當下，進行 BCD 碼判定
                if full_vector <= "1001" then
                    Z <= '1'; -- 0000 ~ 1001 (0~9) 為合法的 BCD 碼，輸出 1
                else
                    Z <= '0'; -- 1010 ~ 1111 (10~15) 為非法，輸出 0
                end if;

            when others =>
                next_state <= S0;
                state_bits <= "00";
                Z          <= '0';
        end case;
    end process;

end Behavioral;
*/
