// Digital circuit 1bit_fulladder_PGC.dig as structural Verilog
module _1bit_fulladder_PGC (
  input  A,
  input  B,
  input  Cin,
  output G,
  output S,
  output P
);

  wire not_1_out, not_2_out, not_3_out;

  not not_1 (not_1_out, A);
  not not_2 (not_2_out, B);
  not not_3 (not_3_out, Cin);
  xor xor_1 (S, A, B, Cin);
  and and_1 (G, A, B);
  xor xor_2 (P, A, B);
endmodule
