// Digital circuit 4bit_adder_cla.dig as structural Verilog
module _4bit_adder_cla (
  input  A0,
  input  B0,
  input  A1,
  input  B1,
  input  A2,
  input  B2,
  input  A3,
  input  B3,
  input  Cin,
  output S0,
  output S1,
  output S2,
  output S3,
  output Cout,
  output S0_2,
  output S1_2,
  output S2_2,
  output S3_2,
  output Cout_2
);

  wire cla_1_c1, cla_1_c2, cla_1_c3, undriven, undriven_2, undriven_3, undriven_4, undriven_5, undriven_6,
       undriven_7, undriven_8;

  _1bit_fulladder _1bit_fulladder_1 ();
  _1bit_fulladder _1bit_fulladder_2 ();
  _1bit_fulladder _1bit_fulladder_3 ();
  _1bit_fulladder _1bit_fulladder_4 ();
  _1bit_fulladder_PGC _1bit_fulladder_pgc_1 ();
  _1bit_fulladder_PGC _1bit_fulladder_pgc_2 ();
  _1bit_fulladder_PGC _1bit_fulladder_pgc_3 ();
  _1bit_fulladder_PGC _1bit_fulladder_pgc_4 ();
  CLA cla_1 (
    .C0(Cin), .G0(undriven_7), .G1(undriven_5), .G2(undriven_2), .G3(undriven_4), .P0(undriven_8),
    .P1(undriven_6), .P2(undriven), .P3(undriven_3), .C1(cla_1_c1), .C2(cla_1_c2), .C3(cla_1_c3), .C4(Cout_2));
endmodule
