// Digital circuit 4bit_adder_subtractor.dig as structural Verilog
module _4bit_adder_subtractor (
  input  A0,
  input  A1,
  input  A2,
  input  A3,
  input  Cin,
  input  B0,
  input  B1,
  input  B2,
  input  B3,
  output Cout,
  output S3,
  output S2,
  output S1,
  output S0
);

  wire xor_1_out, xor_2_out, xor_3_out, xor_4_out;

  xor xor_1 (xor_1_out, B0, Cin);
  xor xor_2 (xor_2_out, B1, Cin);
  xor xor_3 (xor_3_out, B2, Cin);
  xor xor_4 (xor_4_out, B3, Cin);
  _1bit_fulladder _1bit_fulladder_1 ();
  _1bit_fulladder _1bit_fulladder_2 ();
  _1bit_fulladder _1bit_fulladder_3 ();
  _1bit_fulladder _1bit_fulladder_4 ();
endmodule
