// Digital circuit decoder.dig as structural Verilog
module decoder (
  input  A0,
  input  A1,
  input  A2,
  input  A3,
  input  B0,
  input  B1,
  input  B2,
  input  B3,
  input  Cin,
  output LED
);

  wire _4bit_adder_subtractor_1_s0, _4bit_adder_subtractor_1_s1, _4bit_adder_subtractor_1_s2,
       _4bit_adder_subtractor_1_s3, _7seg_1_a, _7seg_1_b, _7seg_1_c, _7seg_1_d, _7seg_1_e, _7seg_1_f,
       _7seg_1_g, and_1_out, and_2_out, not_1_out, not_2_out, not_3_out, not_4_out, not_5_out, not_6_out,
       not_7_out, not_8_out, not_9_out, not_10_out, not_11_out, notconnected_1_out, notconnected_2_out,
       notconnected_3_out, notconnected_4_out, notconnected_5_out, notconnected_6_out, notconnected_7_out,
       notconnected_8_out, xor_1_out;

  xor xor_1 (xor_1_out, Cin, B3);
  _4bit_adder_subtractor _4bit_adder_subtractor_1 (
    .A0(A0), .A1(A1), .A2(A2), .A3(A3), .Cin(Cin), .B0(B0), .B1(B1), .B2(B2), .B3(B3),
    .S3(_4bit_adder_subtractor_1_s3), .S2(_4bit_adder_subtractor_1_s2), .S1(_4bit_adder_subtractor_1_s1),
    .S0(_4bit_adder_subtractor_1_s0));  // open: Cout
  not not_1 (not_1_out, xor_1_out);
  and and_1 (and_1_out, not_1_out, not_2_out, _4bit_adder_subtractor_1_s3);
  not not_2 (not_2_out, A3);
  and and_2 (and_2_out, A3, xor_1_out, not_3_out);
  not not_3 (not_3_out, _4bit_adder_subtractor_1_s3);
  _7seg _7seg_1 (
    .S3(_4bit_adder_subtractor_1_s3), .S2(_4bit_adder_subtractor_1_s2), .S1(_4bit_adder_subtractor_1_s1),
    .S0(_4bit_adder_subtractor_1_s0), .a(_7seg_1_a), .b(_7seg_1_b), .c(_7seg_1_c), .d(_7seg_1_d),
    .e(_7seg_1_e), .f(_7seg_1_f), .g(_7seg_1_g));
  or or_1 (LED, and_1_out, and_2_out);
  // NotConnected on notconnected_1_out
  Seven_Seg #(.commonCathode("true"), .commonConnectionType("anode")) seven_seg_1 (
    .a(notconnected_1_out), .b(notconnected_3_out), .c(notconnected_4_out), .d(notconnected_5_out),
    .e(notconnected_2_out), .f(notconnected_7_out), .g(not_4_out), .dp(notconnected_6_out), .common(1'b1));
  not not_4 (not_4_out, _4bit_adder_subtractor_1_s3);
  // NotConnected on notconnected_2_out
  // NotConnected on notconnected_3_out
  // NotConnected on notconnected_4_out
  // NotConnected on notconnected_5_out
  // NotConnected on notconnected_6_out
  // NotConnected on notconnected_7_out
  not not_5 (not_5_out, _7seg_1_a);
  Seven_Seg #(.commonCathode("true"), .commonConnectionType("anode")) seven_seg_2 (
    .a(not_5_out), .b(not_7_out), .c(not_8_out), .d(not_9_out), .e(not_6_out), .f(not_10_out),
    .g(not_11_out), .dp(notconnected_8_out), .common(1'b1));
  not not_6 (not_6_out, _7seg_1_e);
  not not_7 (not_7_out, _7seg_1_b);
  not not_8 (not_8_out, _7seg_1_c);
  not not_9 (not_9_out, _7seg_1_d);
  // NotConnected on notconnected_8_out
  not not_10 (not_10_out, _7seg_1_f);
  not not_11 (not_11_out, _7seg_1_g);
endmodule
