// Digital circuit decoder_output.dig as structural Verilog
module decoder_output (
  input  A0,
  input  A1,
  input  A2,
  input  A3,
  input  B0,
  input  B1,
  input  B2,
  input  B3,
  input  Cin,
  output LED,
  output a,
  output b,
  output c,
  output d,
  output e,
  output f,
  output g,
  output sign
);

  wire _4bit_adder_subtractor_1_s0, _4bit_adder_subtractor_1_s1, _4bit_adder_subtractor_1_s2,
       _4bit_adder_subtractor_1_s3, _7seg_1_a, _7seg_1_b, _7seg_1_c, _7seg_1_d, _7seg_1_e, _7seg_1_f,
       _7seg_1_g, and_1_out, and_2_out, not_1_out, not_2_out, not_3_out, xor_1_out;

  xor xor_1 (xor_1_out, Cin, B3);
  _4bit_adder_subtractor _4bit_adder_subtractor_1 (
    .A0(A0), .A1(A1), .A2(A2), .A3(A3), .Cin(Cin), .B0(B0), .B1(B1), .B2(B2), .B3(B3),
    .S3(_4bit_adder_subtractor_1_s3), .S2(_4bit_adder_subtractor_1_s2), .S1(_4bit_adder_subtractor_1_s1),
    .S0(_4bit_adder_subtractor_1_s0));  // open: Cout
  not not_1 (not_1_out, xor_1_out);
  and and_1 (and_1_out, not_1_out, not_2_out, _4bit_adder_subtractor_1_s3);
  not not_2 (not_2_out, A3);
  and and_2 (and_2_out, A3, xor_1_out, not_3_out);
  not not_3 (not_3_out, _4bit_adder_subtractor_1_s3);
  _7seg _7seg_1 (
    .S3(_4bit_adder_subtractor_1_s3), .S2(_4bit_adder_subtractor_1_s2), .S1(_4bit_adder_subtractor_1_s1),
    .S0(_4bit_adder_subtractor_1_s0), .a(_7seg_1_a), .b(_7seg_1_b), .c(_7seg_1_c), .d(_7seg_1_d),
    .e(_7seg_1_e), .f(_7seg_1_f), .g(_7seg_1_g));
  or or_1 (LED, and_1_out, and_2_out);
  not not_4 (sign, _4bit_adder_subtractor_1_s3);
  not not_5 (a, _7seg_1_a);
  not not_6 (e, _7seg_1_e);
  not not_7 (b, _7seg_1_b);
  not not_8 (c, _7seg_1_c);
  not not_9 (d, _7seg_1_d);
  not not_10 (f, _7seg_1_f);
  not not_11 (g, _7seg_1_g);
endmodule
