// Digital circuit 9dckt _output.dig as structural Verilog
module _9dckt__output (
  input  A,
  input  B,
  input  C,
  input  D,
  output a_2,
  output b_2,
  output c_2,
  output d_2,
  output e,
  output f,
  output g,
  output W,
  output X,
  output Y,
  output Z
);

  wire undriven, undriven_2, undriven_3, undriven_4, undriven_5, undriven_6, undriven_7;

  NOR_ckt nor_ckt_1 ();
  seven_segment seven_segment_1 ();
  not not_1 (a_2, undriven_5);
  not not_2 (b_2, undriven_7);
  not not_3 (c_2, undriven_6);
  not not_4 (d_2, undriven_4);
  not not_5 (e, undriven_3);
  not not_6 (f, undriven_2);
  not not_7 (g, undriven);
endmodule
