// Digital circuit 9dckt.dig as structural Verilog
module _9dckt (
  input  A,
  input  B,
  input  C,
  input  D,
  output W,
  output X,
  output Y,
  output Z
);

  wire not_1_out, not_2_out, not_3_out, not_4_out, not_5_out, not_6_out, not_7_out, notconnected_1_out,
       undriven, undriven_2, undriven_3, undriven_4, undriven_5, undriven_6, undriven_7;

  NOR_ckt nor_ckt_1 ();
  seven_segment seven_segment_1 ();
  not not_1 (not_1_out, undriven_5);
  not not_2 (not_2_out, undriven_7);
  not not_3 (not_3_out, undriven_6);
  not not_4 (not_4_out, undriven_4);
  Seven_Seg #(.commonCathode("true"), .commonConnectionType("anode")) seven_seg_1 (
    .a(not_1_out), .b(not_2_out), .c(not_3_out), .d(not_4_out), .e(not_5_out), .f(not_6_out), .g(not_7_out),
    .dp(notconnected_1_out), .common(1'b1));
  not not_5 (not_5_out, undriven_3);
  not not_6 (not_6_out, undriven_2);
  not not_7 (not_7_out, undriven);
  // NotConnected on notconnected_1_out
endmodule
