// Digital circuit NOR_ckt.dig as structural Verilog
module NOR_ckt (
  input  A,
  input  B,
  input  C,
  input  D,
  output W,
  output X,
  output Y,
  output Z
);

  wire nor_1_out, nor_2_out, nor_3_out, nor_4_out, nor_6_out, nor_7_out, nor_8_out, nor_9_out, nor_10_out,
       nor_11_out;

  nor nor_1 (nor_1_out, A, A);
  nor nor_2 (nor_2_out, B, B);
  nor nor_3 (nor_3_out, C, C);
  nor nor_4 (nor_4_out, D, D);
  nor nor_5 (W, A, B, C);
  nor nor_6 (nor_6_out, B, nor_3_out);
  nor nor_7 (nor_7_out, nor_2_out, C);
  nor nor_8 (nor_8_out, A, D);
  nor nor_9 (nor_9_out, B, D);
  nor nor_10 (nor_10_out, nor_6_out, nor_7_out);
  nor nor_11 (nor_11_out, nor_8_out, nor_9_out);
  nor nor_12 (X, nor_10_out, nor_10_out);
  nor nor_13 (Z, nor_11_out, nor_11_out);

  assign Y = C;
endmodule
