// Digital circuit Nined_Decorder.dig as structural Verilog
module Nined_Decorder (
  input  [3:0] Input,
  output W,
  output X,
  output Y,
  output Z
);

  wire decoder_1_out_0, decoder_1_out_1, decoder_1_out_2, decoder_1_out_3, decoder_1_out_4, decoder_1_out_5,
       decoder_1_out_6, decoder_1_out_7, decoder_1_out_8, decoder_1_out_9, decoder_1_out_10,
       decoder_1_out_11, decoder_1_out_12, decoder_1_out_13, decoder_1_out_14, decoder_1_out_15;

  Decoder #(.Selector_Bits(4)) decoder_1 (
    .sel(Input), .out_0(decoder_1_out_0), .out_1(decoder_1_out_1), .out_2(decoder_1_out_2),
    .out_3(decoder_1_out_3), .out_4(decoder_1_out_4), .out_5(decoder_1_out_5), .out_6(decoder_1_out_6),
    .out_7(decoder_1_out_7), .out_8(decoder_1_out_8), .out_9(decoder_1_out_9), .out_10(decoder_1_out_10),
    .out_11(decoder_1_out_11), .out_12(decoder_1_out_12), .out_13(decoder_1_out_13),
    .out_14(decoder_1_out_14), .out_15(decoder_1_out_15));
  or or_1 (W, decoder_1_out_1, decoder_1_out_0);
  or or_2 (X, decoder_1_out_5, decoder_1_out_4, decoder_1_out_3, decoder_1_out_2);
  or or_3 (Y, decoder_1_out_7, decoder_1_out_6, decoder_1_out_3, decoder_1_out_2);
  or or_4 (Z, decoder_1_out_8, decoder_1_out_6, decoder_1_out_4, decoder_1_out_2, decoder_1_out_0);
endmodule
