// Digital circuit Nined_ROM.dig as structural Verilog
module Nined_ROM (
  input  Enable,
  input  [3:0] Input,
  output [3:0] Output
);

  ROM #(.AddrBits(4), .Bits(4)) _9_d (.A(Input), .sel(Enable), .D(Output));

  // Notes on the sheet:
  //   contents of _9_d (hex, n*v repeats v):
  //   9,8,7,6,5,4,3,2,1
endmodule
