// Digital circuit comparator_4in_2out.dig as structural Verilog
module comparator_4in_2out (
  input  A0,
  input  A1,
  input  A2,
  input  A3,
  input  B0,
  input  B1,
  input  B2,
  input  B3,
  output A_is_bigger,
  output B_is_bigger
);

  wire _1bit_comparator_1_ao, _1bit_comparator_1_bo, _1bit_comparator_2_ao, _1bit_comparator_2_bo,
       _1bit_comparator_3_ao, _1bit_comparator_3_bo;

  _1bit_comparator _1bit_comparator_1 (
    .Ab(1'b0), .Bb(1'b0), .Ain(A3), .Bin(B3), .Ao(_1bit_comparator_1_ao), .Bo(_1bit_comparator_1_bo));
  _1bit_comparator _1bit_comparator_2 (
    .Ab(_1bit_comparator_1_ao), .Bb(_1bit_comparator_1_bo), .Ain(A2), .Bin(B2), .Ao(_1bit_comparator_2_ao),
    .Bo(_1bit_comparator_2_bo));
  _1bit_comparator _1bit_comparator_3 (
    .Ab(_1bit_comparator_2_ao), .Bb(_1bit_comparator_2_bo), .Ain(A1), .Bin(B1), .Ao(_1bit_comparator_3_ao),
    .Bo(_1bit_comparator_3_bo));
  _1bit_comparator _1bit_comparator_4 (
    .Ab(_1bit_comparator_3_ao), .Bb(_1bit_comparator_3_bo), .Ain(A0), .Bin(B0), .Ao(A_is_bigger),
    .Bo(B_is_bigger));
endmodule
