// Digital circuit fulladder4_2.dig as structural Verilog
module fulladder4_2 (
  input  [3:0] in_3,
  input  [3:0] in_4,
  input  in_5,
  input  in_6,
  output [3:0] out_1,
  output out_2
);

  FullAdder4 #(.applicationType("GHDL")) u_FullAdder4 (
    .A(in_3), .B(in_4), .Ci(in_5), .Sub(in_6), .S(out_1), .Co(out_2));
endmodule

/* Code of FullAdder4:
LIBRARY ieee;
USE ieee.std_logic_1164.all;
USE ieee.numeric_std.all;

entity FullAdder4 is
port (
   	A, B: in std_logic_vector(3 downto 0);
    	Ci: in std_logic;
	Sub: in std_logic;
    	S: out std_logic_vector(3 downto 0);
    	Co: out std_logic);
end FullAdder4;

architecture Structure of FullAdder4 is
component FullAdder
	port (	A, B, Cin, Sub: in std_logic;
		Cout, Sum: out std_logic );
end component;

signal C: std_logic_vector(3 downto 1);
begin
	FA0: FullAdder port map(A(0), B(0), Ci, Sub, C(1), S(0));
	FA1: FullAdder port map(A(1), B(1), C(1), Sub, C(2), S(1));
	FA2: FullAdder port map(A(2), B(2), C(2), Sub, C(3), S(2));
	FA3: FullAdder port map(A(3), B(3), C(3), Sub, Co, S(3));
end Structure;

LIBRARY ieee;
USE ieee.std_logic_1164.all;
USE ieee.numeric_std.all;

entity FullAdder is
  port (
    A, B, Cin, Sub: in std_logic;
    Sum, Cout: out std_logic);
end FullAdder;

architecture Equations of FullAdder is
begin
	-- concurrent assignment statements

	Sum <= 	(not A and not B and Cin) or
		(not A and B and not Cin) or
           	(A and not B and not Cin) or
           	(A and B and Cin);
	Cout <= (not A and Cin and Sub) or
            	(not A and B and Sub) or
            	(A and Cin and not Sub) or
            	(A and B and not Sub) or
            	(B and Cin);
end Equations;
*/
