// Digital circuit truthtable.dig as structural Verilog
module truthtable (
  input  A,
  input  B,
  input  Cin,
  input  Sub,
  output Cout,
  output Sum
);

  wire and_1_out, and_2_out, and_3_out, and_4_out, and_5_out, and_6_out, and_7_out, and_8_out, and_9_out,
       not_1_out, not_2_out, not_3_out, not_4_out;

  not not_1 (not_1_out, A);
  not not_2 (not_2_out, B);
  not not_3 (not_3_out, Cin);
  not not_4 (not_4_out, Sub);
  and and_1 (and_1_out, not_1_out, Cin, Sub);
  and and_2 (and_2_out, not_1_out, B, Sub);
  and and_3 (and_3_out, A, Cin, not_4_out);
  and and_4 (and_4_out, A, B, not_4_out);
  and and_5 (and_5_out, B, Cin);
  and and_6 (and_6_out, not_1_out, not_2_out, Cin);
  and and_7 (and_7_out, not_1_out, B, not_3_out);
  and and_8 (and_8_out, A, not_2_out, not_3_out);
  and and_9 (and_9_out, A, B, Cin);
  or or_1 (Cout, and_1_out, and_2_out, and_3_out, and_4_out, and_5_out);
  or or_2 (Sum, and_6_out, and_7_out, and_8_out, and_9_out);
endmodule
