// Digital circuit SRlatch_1.dig as structural Verilog
module SRlatch_1 (
  input  S,
  input  R,
  input  CLK,
  output Q,
  output Q_2
);

  wire and_1_out, and_2_out, and_3_out, and_4_out, not_1_out, undriven, undriven_2;

  not not_1 (not_1_out, CLK);
  and and_1 (and_1_out, S, not_1_out);
  and and_2 (and_2_out, not_1_out, R);
  SRlatch_nor srlatch_nor_1 ();
  and and_3 (and_3_out, undriven_2, CLK);
  and and_4 (and_4_out, undriven, CLK);
  SRlatch_nor srlatch_nor_2 ();
endmodule
