// Digital circuit SRlatch_2.dig as structural Verilog
module SRlatch_2 (
  input  S,
  input  R,
  input  CLK,
  output Q,
  output Q_2
);

  wire and_1_out, and_2_out, and_3_out, and_4_out, and_5_out, and_6_out, not_1_out, undriven, undriven_2;

  not not_1 (not_1_out, CLK);
  and and_1 (and_1_out, S, not_1_out);
  and and_2 (and_2_out, not_1_out, R);
  SRlatch_nor srlatch_nor_1 ();
  and and_3 (and_3_out, S, undriven_2);
  and and_4 (and_4_out, undriven, R);
  and and_5 (and_5_out, and_3_out, CLK);
  and and_6 (and_6_out, and_4_out, CLK);
  SRlatch_nor srlatch_nor_2 ();
endmodule
