// Digital circuit SRlatch_vhdl.dig as structural Verilog
module SRlatch_vhdl (
  input  S,
  input  R,
  input  CLK,
  output Q,
  output Q_2
);

  SRFF #(.applicationType("GHDL"), .Code_File("C:\\Users\\User-010855\\Downloads\\Lab06\\lab6.vhdl")) u_SRFF (
    .S(S), .R(R), .CLK(CLK), .Q(Q), .QN(Q_2));
endmodule

/* Code of SRFF:
LIBRARY ieee;
USE ieee.std_logic_1164.all;
USE ieee.numeric_std.all;

entity SRFF is
port (S, R, CLK: in std_logic;
      Q, QN: out std_logic);	
end SRFF;

architecture SRFF1 of SRFF is
signal Qint: std_logic:='0';

begin
	Q <= Qint;	-- output Q and QN to port
	QN <= not Qint;	
	process (CLK)	
	begin
		if CLK'event and CLK = '1' then
			if S='0' and R='0' then  Qint <= Qint;
			elsif S='1' and R='0' then  Qint <= '1'; 
			elsif S='0' and R='1' then  Qint <= '0';  
			end if;
		end if;
	 end process;
end SRFF1;
*/
