// Digital circuit 1bit_comparator.dig as structural Verilog
module _1bit_comparator (
  input  Ab,
  input  Bb,
  input  Ain,
  input  Bin,
  output Ao,
  output Bo
);

  wire and_1_out, and_2_out, not_1_out, not_2_out, not_3_out, not_4_out;

  not not_1 (not_1_out, Ab);
  not not_2 (not_2_out, Bb);
  not not_3 (not_3_out, Ain);
  not not_4 (not_4_out, Bin);
  and and_1 (and_1_out, Ain, not_4_out, not_2_out);
  and and_2 (and_2_out, not_3_out, Bin, not_1_out);
  or or_1 (Ao, and_1_out, Ab);
  or or_2 (Bo, and_2_out, Bb);
endmodule
