// Digital circuit 4bit_adder_subtractor.dig as structural Verilog
module _4bit_adder_subtractor (
  input  C,
  input  [3:0] B,
  input  [3:0] A,
  output Co,
  output [3:0] S
);

  wire xor_1_out, xor_2_out, xor_3_out, xor_4_out;

  xor xor_1 (xor_1_out, B[0], C);
  xor xor_2 (xor_2_out, B[1], C);
  xor xor_3 (xor_3_out, B[2], C);
  xor xor_4 (xor_4_out, B[3], C);
  _1bit_fulladder _1bit_fulladder_1 ();
  _1bit_fulladder _1bit_fulladder_2 ();
  _1bit_fulladder _1bit_fulladder_3 ();
  _1bit_fulladder _1bit_fulladder_4 ();
endmodule
