// Digital circuit comparator.dig as structural Verilog
module comparator (
  input  [3:0] A,
  input  [3:0] B,
  output Ao,
  output Bo
);

  wire _1bit_comparator_1_ao, _1bit_comparator_1_bo, _1bit_comparator_2_ao, _1bit_comparator_2_bo,
       _1bit_comparator_3_ao, _1bit_comparator_3_bo;

  _1bit_comparator _1bit_comparator_1 (
    .Ab(1'b0), .Bb(1'b0), .Ain(A[3]), .Bin(B[3]), .Ao(_1bit_comparator_1_ao), .Bo(_1bit_comparator_1_bo));
  _1bit_comparator _1bit_comparator_2 (
    .Ab(_1bit_comparator_1_ao), .Bb(_1bit_comparator_1_bo), .Ain(A[2]), .Bin(B[2]),
    .Ao(_1bit_comparator_2_ao), .Bo(_1bit_comparator_2_bo));
  _1bit_comparator _1bit_comparator_3 (
    .Ab(_1bit_comparator_2_ao), .Bb(_1bit_comparator_2_bo), .Ain(A[1]), .Bin(B[1]),
    .Ao(_1bit_comparator_3_ao), .Bo(_1bit_comparator_3_bo));
  _1bit_comparator _1bit_comparator_4 (
    .Ab(_1bit_comparator_3_ao), .Bb(_1bit_comparator_3_bo), .Ain(A[0]), .Bin(B[0]), .Ao(Ao), .Bo(Bo));
endmodule
