// Digital circuit HW2_1.dig as structural Verilog
module HW2_1 (
  input  x,
  input  clk,
  output S2,
  output S1,
  output S0,
  output z
);

  state_machine #(.applicationType("GHDL")) u_state_machine (.clk(clk), .x(x), .z(z), .q_out({S2, S1, S0}));
endmodule

/* Code of state_machine:
library IEEE;
use IEEE.STD_LOGIC_1164.ALL;

entity state_machine is
    port (
        clk   : in  std_logic;
        x     : in  std_logic;
        z     : out std_logic;
        q_out : out std_logic_vector(2 downto 0) -- 輸出當前狀態 (Q2 Q1 Q0)
    );
end entity state_machine;

architecture rtl of state_machine is

    -- 狀態暫存器 (3 bits)，給予初始值 "000" (S0)
    signal Q : std_logic_vector(2 downto 0) := "000";

    -- 為了提高可讀性，使用別名 (Alias) 對應到暫存器位元
    alias Q2 : std_logic is Q(2);
    alias Q1 : std_logic is Q(1);
    alias Q0 : std_logic is Q(0);

    -- 次態連線 (Next state wires)
    signal Q2n, Q1n, Q0n : std_logic;

begin

    -- --------------------------------------------------------
    -- Combinational Logic (根據卡諾圖化簡得到的布林式)
    -- --------------------------------------------------------

    -- Q2+ = Q1 Q0 X'
    Q2n <= Q1 and Q0 and (not x);

    -- Q1+ = Q2 Q0' X' + Q1' Q0 X' + Q2' Q1' X + Q1 Q0' X
    Q1n <= (Q2 and not Q0 and not x) or 
           (not Q1 and Q0 and not x) or 
           (not Q2 and not Q1 and x) or 
           (Q1 and not Q0 and x);

    -- Q0+ = Q0' X' + Q2' Q0' + Q2' Q1' X
    Q0n <= (not Q0 and not x) or 
           (not Q2 and not Q0) or 
           (not Q2 and not Q1 and x);

    -- Mealy Output: Z = (Q1 + Q2) Q0' X
    z   <= (Q1 or Q2) and (not Q0) and x;

    -- --------------------------------------------------------
    -- Sequential Logic (狀態位移)
    -- --------------------------------------------------------
    process(clk)
    begin
        if rising_edge(clk) then
            -- 在時脈上升沿更新狀態
            Q <= Q2n & Q1n & Q0n;
        end if;
    end process;

    -- 將內部狀態同步輸出給 q_out
    q_out <= Q;

end architecture rtl;
*/
