// Digital circuit hw1.dig as structural Verilog
module hw1 (
  input  clk,
  output out_2,
  output out_3,
  output out_4
);

  wire jk_ff_2_nq, jk_ff_3_nq, or_1_out, or_2_out, or_3_out;

  JK_FF jk_ff_1 (.J(out_4), .C(clk), .K(out_4), .Q(out_2));  // open: nQ
  or or_1 (or_1_out, out_2, jk_ff_3_nq);
  JK_FF jk_ff_2 (.J(or_1_out), .C(clk), .K(or_3_out), .Q(out_3), .nQ(jk_ff_2_nq));
  or or_2 (or_2_out, out_2, out_3);
  or or_3 (or_3_out, jk_ff_2_nq, out_3);
  JK_FF jk_ff_3 (.J(or_2_out), .C(clk), .K(out_3), .Q(out_4), .nQ(jk_ff_3_nq));
endmodule
