// Digital circuit 1bit_fulladder.dig as structural Verilog
module _1bit_fulladder (
  input  A,
  input  B,
  input  Cin,
  output Cout,
  output Sum
);

  wire and_1_out, and_2_out, and_3_out, not_1_out, not_2_out, not_3_out;

  not not_1 (not_1_out, A);
  not not_2 (not_2_out, B);
  not not_3 (not_3_out, Cin);
  xor xor_1 (Sum, A, B, Cin);
  and and_1 (and_1_out, A, B);
  and and_2 (and_2_out, A, Cin);
  and and_3 (and_3_out, B, Cin);
  or or_1 (Cout, and_1_out, and_2_out, and_3_out);
endmodule
