// Digital circuit SRAM_2.dig as structural Verilog
module SRAM_2 (
  input  [3:0] D,
  input  [1:0] Addr,
  input  CS,
  input  OE,
  input  Sel2,
  input  Sel1,
  input  CLK,
  input  En1,
  input  WE,
  input  En2,
  input  En3
);

  wire and_1_out, comparator_1_bo, not_1_out, register_2_q;
  wire [3:0] _4bit_adder_subtractor_1_s, demultiplexer_1_out_0, demultiplexer_1_out_1, multiplexer_1_out,
       register_1_q, register_3_q, u_SRAM_do;

  Register #(.Bits(4)) register_1 (.D(_4bit_adder_subtractor_1_s), .C(CLK), .en(En2), .Q(register_1_q));
  Multiplexer #(.Bits(4)) multiplexer_1 (.sel(Sel2), .in_0(D), .in_1(register_1_q), .out(multiplexer_1_out));
  Register register_2 (.D(comparator_1_bo), .C(CLK), .en(En3), .Q(register_2_q));
  not not_1 (not_1_out, register_2_q);
  and and_1 (and_1_out, not_1_out, WE);
  comparator comparator_1 (
    .A(_4bit_adder_subtractor_1_s), .B(demultiplexer_1_out_1), .Bo(comparator_1_bo));  // open: Ao
  SRAM #(.applicationType("GHDL")) u_SRAM (
    .D(multiplexer_1_out), .Address(Addr), .ChipSelect(CS), .WE(and_1_out), .OE(OE), .DO(u_SRAM_do));
  _4bit_adder_subtractor _4bit_adder_subtractor_1 (
    .C(1'b0), .B(demultiplexer_1_out_1), .A(register_3_q), .S(_4bit_adder_subtractor_1_s));  // open: Co
  Demultiplexer #(.Bits(4)) demultiplexer_1 (
    .sel(Sel1), .in(u_SRAM_do), .out_0(demultiplexer_1_out_0), .out_1(demultiplexer_1_out_1));
  Register #(.Bits(4)) register_3 (.D(demultiplexer_1_out_0), .C(CLK), .en(En1), .Q(register_3_q));
endmodule

/* Code of SRAM:
LIBRARY ieee;
USE ieee.std_logic_1164.all;
USE ieee.numeric_std.all;

entity SRAM is
port (	
    D: in std_logic_vector(3 downto 0);      -- 資料輸入
    Address: in std_logic_vector(1 downto 0); -- 改為 2-bit 以定址 4 組 (00, 01, 10, 11)
    ChipSelect, WE, OE: in std_logic;
    DO: out std_logic_vector(3 downto 0)     -- 資料輸出
);
end SRAM;

architecture SRAM_simple of SRAM is

    -- 定義記憶體：4 個元素，每個元素是 4 位元的向量
    type memory is array (0 to 3) of std_logic_vector(3 downto 0);
    signal SRAM_internal: memory := (others => "0000");

begin

    -- 寫入邏輯：當 CS=1 且 WE=1 時寫入
    process(ChipSelect, WE, Address, D)
    begin
        if (ChipSelect = '1' and WE = '1') then
            SRAM_internal(to_integer(unsigned(Address))) <= D;
        end if;
    end process;

    -- 讀取邏輯：當 CS=1, OE=1 且 WE=0 時輸出資料，其餘狀態輸出高阻抗 (Hi-Z)
    DO <= SRAM_internal(to_integer(unsigned(Address))) 
          when (ChipSelect = '1' and OE = '1' and WE = '0') 
          else "ZZZZ";

end SRAM_simple;
*/
