// Digital circuit SRAM_3.dig as structural Verilog
module SRAM_3 (
  input  [3:0] D,
  input  rst,
  input  clk,
  output [1:0] S3,
  output S2,
  output S1,
  output S0,
  output [3:0] DO
);

  wire u_CtrSRAM_en1, u_CtrSRAM_en2, u_CtrSRAM_sel1, u_CtrSRAM_sel2;
  wire [3:0] _4bit_adder_subtractor_1_s, demultiplexer_1_out_0, demultiplexer_1_out_1, multiplexer_1_out,
       register_1_q, register_2_q;

  Register #(.Bits(4)) register_1 (.D(_4bit_adder_subtractor_1_s), .C(clk), .en(u_CtrSRAM_en2), .Q(register_1_q));
  Multiplexer #(.Bits(4)) multiplexer_1 (.sel(u_CtrSRAM_sel2), .in_0(D), .in_1(register_1_q), .out(multiplexer_1_out));
  SRAM #(.applicationType("GHDL")) u_SRAM (
    .D(multiplexer_1_out), .Address(S3), .ChipSelect(S2), .WE(S1), .OE(S0), .DO(DO));
  _4bit_adder_subtractor _4bit_adder_subtractor_1 (
    .C(1'b0), .B(demultiplexer_1_out_1), .A(register_2_q), .S(_4bit_adder_subtractor_1_s));  // open: Co
  CtrSRAM #(.applicationType("GHDL")) u_CtrSRAM (
    .clk(clk), .rst(rst), .sel1(u_CtrSRAM_sel1), .en1(u_CtrSRAM_en1), .sel2(u_CtrSRAM_sel2),
    .en2(u_CtrSRAM_en2), .Addr(S3), .CS(S2), .WE(S1), .OE(S0));
  Demultiplexer #(.Bits(4)) demultiplexer_1 (
    .sel(u_CtrSRAM_sel1), .in(DO), .out_0(demultiplexer_1_out_0), .out_1(demultiplexer_1_out_1));
  Register #(.Bits(4)) register_2 (.D(demultiplexer_1_out_0), .C(clk), .en(u_CtrSRAM_en1), .Q(register_2_q));
endmodule

/* Code of SRAM:
LIBRARY ieee;
USE ieee.std_logic_1164.all;
USE ieee.numeric_std.all;

entity SRAM is
port (	
    D: in std_logic_vector(3 downto 0);
    Address: in std_logic_vector(1 downto 0);
    ChipSelect, WE, OE: in std_logic;
    DO: out std_logic_vector(3 downto 0)
);
end SRAM;

architecture SRAM_simple of SRAM is
    type memory is array (0 to 3) of std_logic_vector(3 downto 0);
    signal SRAM_internal: memory := (others => "0000");
begin
    -- 寫入邏輯：CS=1 且 WE=1 時寫入（不管 OE 狀態）
    process(ChipSelect, WE, Address, D)
    begin
        if (ChipSelect = '1' and WE = '1') then
            SRAM_internal(to_integer(unsigned(Address))) <= D;
        end if;
    end process;

    -- 讀取邏輯：CS=1 且 OE=1 時輸出（WE=1 同時寫入也能讀出，即 write-through）
    DO <= SRAM_internal(to_integer(unsigned(Address)))
          when (ChipSelect = '1' and OE = '1')
          else "ZZZZ";
end SRAM_simple;
*/

/* Code of CtrSRAM:
LIBRARY ieee;
USE ieee.std_logic_1164.all;

entity CtrSRAM is
    port (
        clk  : in  std_logic;
        rst  : in  std_logic;
        sel1 : out std_logic;
        en1  : out std_logic;
        sel2 : out std_logic;
        en2  : out std_logic;
        Addr : out std_logic_vector(1 downto 0);
        CS   : out std_logic;
        WE   : out std_logic;
        OE   : out std_logic
    );
end CtrSRAM;

architecture CtrSRAM_arch of CtrSRAM is
    type state_type is (S0, S1, S2, S3, S4, S5);
    signal current_state, next_state : state_type;
begin

    -- ==========================================
    -- 狀態暫存器（同步 reset）
    -- ==========================================
    process(clk)
    begin
        if rising_edge(clk) then
            if rst = '1' then
                current_state <= S0;   -- 同步 reset 回 S0
            else
                current_state <= next_state;
            end if;
        end if;
    end process;

    -- ==========================================
    -- 次態邏輯（rst 加入敏感列，S0 等 rst 放開）
    -- ==========================================
    process(current_state, rst)
    begin
        case current_state is
            when S0 =>
                if rst = '1' then
                    next_state <= S0;   -- rst 期間鎖在 S0
                else
                    next_state <= S1;   -- rst 放開才往前
                end if;
            when S1 => next_state <= S2;
            when S2 => next_state <= S3;
            when S3 => next_state <= S4;
            when S4 => next_state <= S5;
            when S5 => next_state <= S5;
            when others => next_state <= S0;
        end case;
    end process;

    -- ==========================================
    -- 輸出邏輯（Moore）
    -- ==========================================
    process(current_state)
    begin
        sel1 <= '0'; en1 <= '0'; sel2 <= '0'; en2 <= '0';
        Addr <= "00"; CS <= '0'; WE <= '0'; OE <= '0';

        case current_state is
            when S0 =>
                sel1 <= '0'; en1 <= '0'; sel2 <= '0'; en2 <= '0';
                Addr <= "00"; CS <= '0'; WE <= '0'; OE <= '0';
            when S1 =>
                sel1 <= '0'; en1 <= '0'; sel2 <= '0'; en2 <= '0';
                Addr <= "00"; CS <= '1'; WE <= '1'; OE <= '0';
            when S2 =>
                sel1 <= '0'; en1 <= '0'; sel2 <= '0'; en2 <= '0';
                Addr <= "01"; CS <= '1'; WE <= '1'; OE <= '0';
            when S3 =>
                sel1 <= '0'; en1 <= '1'; sel2 <= '0'; en2 <= '0';
                Addr <= "00"; CS <= '1'; WE <= '0'; OE <= '1';
            when S4 =>
                sel1 <= '1'; en1 <= '0'; sel2 <= '1'; en2 <= '1';
                Addr <= "01"; CS <= '1'; WE <= '0'; OE <= '1';
            when S5 =>
                sel1 <= '1'; en1 <= '0'; sel2 <= '1'; en2 <= '1';
                Addr <= "01"; CS <= '1'; WE <= '1'; OE <= '1';
            when others =>
                null;
        end case;
    end process;

end CtrSRAM_arch;
*/
