// Digital circuit SRAM_4.dig as structural Verilog
module SRAM_4 (
  input  [3:0] D,
  input  rst,
  input  clk,
  output [1:0] S3,
  output S2,
  output S1,
  output S0,
  output [3:0] DO
);

  wire u_CtrSRAM_2_en1, u_CtrSRAM_2_en2, u_CtrSRAM_2_sel1, u_CtrSRAM_2_sel2;
  wire [3:0] _4bit_adder_subtractor_1_s, demultiplexer_1_out_0, demultiplexer_1_out_1, multiplexer_1_out,
       register_1_q, register_2_q;

  Register #(.Bits(4)) register_1 (.D(_4bit_adder_subtractor_1_s), .C(clk), .en(u_CtrSRAM_2_en2), .Q(register_1_q));
  Multiplexer #(.Bits(4)) multiplexer_1 (
    .sel(u_CtrSRAM_2_sel2), .in_0(D), .in_1(register_1_q), .out(multiplexer_1_out));
  SRAM #(.applicationType("GHDL")) u_SRAM (
    .D(multiplexer_1_out), .Address(S3), .ChipSelect(S2), .WE(S1), .OE(S0), .DO(DO));
  _4bit_adder_subtractor _4bit_adder_subtractor_1 (
    .C(1'b0), .B(demultiplexer_1_out_1), .A(register_2_q), .S(_4bit_adder_subtractor_1_s));  // open: Co
  CtrSRAM_2 #(.applicationType("GHDL")) u_CtrSRAM_2 (
    .clk(clk), .rst(rst), .sel1(u_CtrSRAM_2_sel1), .en1(u_CtrSRAM_2_en1), .sel2(u_CtrSRAM_2_sel2),
    .en2(u_CtrSRAM_2_en2), .Addr(S3), .CS(S2), .WE(S1), .OE(S0));
  Demultiplexer #(.Bits(4)) demultiplexer_1 (
    .sel(u_CtrSRAM_2_sel1), .in(DO), .out_0(demultiplexer_1_out_0), .out_1(demultiplexer_1_out_1));
  Register #(.Bits(4)) register_2 (.D(demultiplexer_1_out_0), .C(clk), .en(u_CtrSRAM_2_en1), .Q(register_2_q));
endmodule

/* Code of SRAM:
LIBRARY ieee;
USE ieee.std_logic_1164.all;
USE ieee.numeric_std.all;

entity SRAM is
port (	
    D: in std_logic_vector(3 downto 0);
    Address: in std_logic_vector(1 downto 0);
    ChipSelect, WE, OE: in std_logic;
    DO: out std_logic_vector(3 downto 0)
);
end SRAM;

architecture SRAM_simple of SRAM is
    type memory is array (0 to 3) of std_logic_vector(3 downto 0);
    signal SRAM_internal: memory := (others => "0000");
begin
    -- 寫入邏輯：CS=1 且 WE=1 時寫入（不管 OE 狀態）
    process(ChipSelect, WE, Address, D)
    begin
        if (ChipSelect = '1' and WE = '1') then
            SRAM_internal(to_integer(unsigned(Address))) <= D;
        end if;
    end process;

    -- 讀取邏輯：CS=1 且 OE=1 時輸出（WE=1 同時寫入也能讀出，即 write-through）
    DO <= SRAM_internal(to_integer(unsigned(Address)))
          when (ChipSelect = '1' and OE = '1')
          else "ZZZZ";
end SRAM_simple;
*/

/* Code of CtrSRAM_2:
LIBRARY ieee;
USE ieee.std_logic_1164.all;

entity CtrSRAM_2 is
    port (
        clk  : in  std_logic;
        rst  : in  std_logic;
        sel1 : out std_logic;
        en1  : out std_logic;
        sel2 : out std_logic;
        en2  : out std_logic;
        Addr : out std_logic_vector(1 downto 0);
        CS   : out std_logic;
        WE   : out std_logic;
        OE   : out std_logic
    );
end CtrSRAM_2;

architecture Hybrid of CtrSRAM_2 is
    signal Q : std_logic_vector(2 downto 0) := "000"; 
    signal D : std_logic_vector(2 downto 0);
    
    -- 宣告一個 9-bit 的信號，用來當作所有輸出控制線的「總表」
    -- 排列順序：sel1(8), en1(7), sel2(6), en2(5), Addr(4 downto 3), CS(2), WE(1), OE(0)
    signal Ctrl_Bus : std_logic_vector(8 downto 0);

begin

    -- ==========================================
    -- 1. 次態邏輯 (嚴格使用 D 的布林代數式)
    -- ==========================================
    D(2) <= Q(2) or (Q(1) and Q(0));
    D(1) <= (not Q(2) and not Q(1) and Q(0)) or (Q(1) and not Q(0));
    D(0) <= Q(2) or not Q(0);

    -- ==========================================
    -- 2. 狀態暫存器 (D 正反器)
    -- ==========================================
    process(clk)
    begin
        if rising_edge(clk) then
            if rst = '1' then
                Q <= "000"; 
            else
                Q <= D;     
            end if;
        end if;
    end process;

    -- ==========================================
    -- 3. 輸出邏輯 (直接寫成一張真值表 Lookup Table)
    -- ==========================================
    -- 利用 with ... select 語法，根據當前狀態 Q，直接賦值給 Ctrl_Bus
    -- 排列順序: sel1 & en1 & sel2 & en2 & Addr(2 bits) & CS & WE & OE
    with Q select
        Ctrl_Bus <=
            -- sel1, en1, sel2, en2, Addr1, Addr0, CS, WE, OE
            "000000000" when "000", -- S0
            "000000110" when "001", -- S1
            "000001110" when "010", -- S2
            "010000101" when "011", -- S3
            "101101101" when "100", -- S4
            "101101111" when "101", -- S5
            "000000000" when others;-- 未使用狀態 S6, S7 預設輸出 0

    -- ==========================================
    -- 4. 將總表的數值解開，接給實際的輸出腳位
    -- ==========================================
    sel1 <= Ctrl_Bus(8);
    en1  <= Ctrl_Bus(7);
    sel2 <= Ctrl_Bus(6);
    en2  <= Ctrl_Bus(5);
    Addr <= Ctrl_Bus(4 downto 3);
    CS   <= Ctrl_Bus(2);
    WE   <= Ctrl_Bus(1);
    OE   <= Ctrl_Bus(0);

end Hybrid;
*/
